// Logisim project DOIS DISPLAYS.circ as structural Verilog: 4 circuits, main circuit main
module main (
  input  in_1,
  input  in_2,
  input  in_3,
  input  in_4
);

  wire decodificador_1_out_5, decodificador_1_out_6, decodificador_1_out_7, decodificador_1_out_8,
       decodificador_1_out_9, decodificador_1_out_10, decodificador_1_out_11, decodificador_1_out_12,
       decodificador_1_out_13, decodificador_1_out_14, decodificador_1_out_15, decodificador_1_out_16,
       decodificador_1_out_17, decodificador_1_out_18;

  decodificador decodificador_1 (
    .in_1(in_1), .in_2(in_2), .in_3(in_3), .in_4(in_4), .out_5(decodificador_1_out_5),
    .out_6(decodificador_1_out_6), .out_7(decodificador_1_out_7), .out_8(decodificador_1_out_8),
    .out_9(decodificador_1_out_9), .out_10(decodificador_1_out_10), .out_11(decodificador_1_out_11),
    .out_12(decodificador_1_out_12), .out_13(decodificador_1_out_13), .out_14(decodificador_1_out_14),
    .out_15(decodificador_1_out_15), .out_16(decodificador_1_out_16), .out_17(decodificador_1_out_17),
    .out_18(decodificador_1_out_18));
  _7_Segment_Display u_7_segment_display_1 (
    .g(decodificador_1_out_18), .f(decodificador_1_out_17), .a(decodificador_1_out_12),
    .b(decodificador_1_out_13), .e(decodificador_1_out_16), .d(decodificador_1_out_15),
    .c(decodificador_1_out_14));  // open: dp
  _7_Segment_Display u_7_segment_display_2 (
    .g(decodificador_1_out_11), .f(decodificador_1_out_10), .a(decodificador_1_out_5),
    .b(decodificador_1_out_6), .e(decodificador_1_out_9), .d(decodificador_1_out_8), .c(decodificador_1_out_7));  // open: dp
endmodule

module decodificador (
  input  in_1,
  input  in_2,
  input  in_3,
  input  in_4,
  output out_5,
  output out_6,
  output out_7,
  output out_8,
  output out_9,
  output out_10,
  output out_11,
  output out_12,
  output out_13,
  output out_14,
  output out_15,
  output out_16,
  output out_17,
  output out_18
);

  Display_Unidades display_unidades_1 (
    .I3(in_1), .I2(in_2), .I1(in_3), .I0(in_4), .A(out_5), .B(out_6), .C(out_7), .D(out_8), .E(out_9),
    .F(out_10), .G(out_11));
  Display_Dezenas display_dezenas_1 (
    .I3(in_1), .I2(in_2), .I1(in_3), .I0(in_4), .A(out_12), .B(out_13), .C(out_14), .D(out_15), .E(out_16),
    .F(out_17), .G(out_18));
endmodule

// dezenas
module Display_Dezenas (
  input  I3,
  input  I2,
  input  I1,
  input  I0,
  output A,
  output B,
  output C,
  output D,
  output E,
  output F,
  output G
);

  wire and_1_out, and_2_out, and_3_out, and_4_out, not_1_out, not_2_out, not_3_out, not_4_out, not_5_out,
       not_6_out, not_7_out, not_8_out, not_9_out, not_10_out, not_11_out, not_12_out;

  not not_1 (not_1_out, I3);
  not not_2 (not_2_out, I2);
  and and_1 (and_1_out, not_2_out, not_3_out);
  not not_3 (not_3_out, I1);
  not not_4 (not_4_out, I3);
  not not_5 (not_5_out, I2);
  and and_2 (and_2_out, not_5_out, not_6_out);
  not not_6 (not_6_out, I1);
  not not_7 (not_7_out, I3);
  not not_8 (not_8_out, I2);
  and and_3 (and_3_out, not_8_out, not_9_out);
  not not_9 (not_9_out, I1);
  not not_10 (not_10_out, I3);
  not not_11 (not_11_out, I2);
  and and_4 (and_4_out, not_11_out, not_12_out);
  not not_12 (not_12_out, I1);
  or or_1 (A, not_1_out, and_1_out);
  or or_2 (D, not_4_out, and_2_out);
  or or_3 (E, not_7_out, and_3_out);
  or or_4 (F, not_10_out, and_4_out);

  assign B = 1'b1;
  assign C = 1'b1;
  assign G = 1'b0;
endmodule

// unidades
module Display_Unidades (
  input  I3,
  input  I2,
  input  I1,
  input  I0,
  output A,
  output B,
  output C,
  output D,
  output E,
  output F,
  output G
);

  wire and_1_out, and_2_out, and_3_out, and_4_out, and_5_out, and_6_out, and_7_out, and_8_out, and_9_out,
       and_10_out, and_11_out, and_12_out, and_13_out, and_14_out, and_15_out, and_16_out, and_17_out,
       and_18_out, and_19_out, and_20_out, and_21_out, and_22_out, and_23_out, and_24_out, and_25_out,
       and_26_out, and_27_out, and_28_out, and_29_out, and_30_out, and_31_out, not_1_out, not_2_out,
       not_3_out, not_4_out, not_5_out, not_6_out, not_7_out, not_8_out, not_9_out, not_10_out, not_11_out,
       not_12_out, not_13_out, not_14_out, not_15_out, not_16_out, not_17_out, not_18_out, not_19_out,
       not_20_out, not_21_out, not_22_out, not_23_out, not_24_out, not_25_out, not_26_out, not_27_out,
       not_28_out, not_29_out, not_30_out, not_31_out, not_32_out, not_33_out, not_34_out, not_35_out,
       not_36_out, not_37_out, not_38_out, not_39_out, not_40_out, not_41_out, not_42_out, not_43_out;

  not not_1 (not_1_out, I2);
  and and_1 (and_1_out, not_1_out, not_2_out);
  not not_2 (not_2_out, I0);
  not not_3 (not_3_out, I3);
  and and_2 (and_2_out, not_3_out, I1);
  and and_3 (and_3_out, I2, I0);
  and and_4 (and_4_out, I3, not_4_out);
  not not_4 (not_4_out, I1);
  not not_5 (not_5_out, I2);
  not not_6 (not_6_out, I1);
  and and_5 (and_5_out, not_6_out, not_7_out);
  not not_7 (not_7_out, I0);
  not not_8 (not_8_out, I3);
  and and_6 (and_6_out, not_8_out, I1, I0);
  and and_7 (and_7_out, I3, not_9_out);
  not not_9 (not_9_out, I1);
  and and_8 (and_8_out, I3, not_10_out);
  not not_10 (not_10_out, I0);
  not not_11 (not_11_out, I3);
  and and_9 (and_9_out, not_11_out, not_12_out);
  not not_12 (not_12_out, I1);
  and and_10 (and_10_out, I2, I1);
  and and_11 (and_11_out, I3, not_13_out);
  not not_13 (not_13_out, I2);
  not not_14 (not_14_out, I2);
  and and_12 (and_12_out, not_14_out, not_15_out);
  not not_15 (not_15_out, I0);
  not not_16 (not_16_out, I3);
  and and_13 (and_13_out, not_16_out, not_17_out, I1);
  not not_17 (not_17_out, I2);
  not not_18 (not_18_out, I3);
  and and_14 (and_14_out, not_18_out, I1, not_19_out);
  not not_19 (not_19_out, I0);
  and and_15 (and_15_out, I2, not_20_out, I0);
  not not_20 (not_20_out, I1);
  and and_16 (and_16_out, I3, not_21_out);
  not not_21 (not_21_out, I1);
  and and_17 (and_17_out, I3, I2, I0);
  not not_22 (not_22_out, I2);
  and and_18 (and_18_out, not_22_out, not_23_out);
  not not_23 (not_23_out, I0);
  not not_24 (not_24_out, I3);
  and and_19 (and_19_out, not_24_out, I1, not_25_out);
  not not_25 (not_25_out, I0);
  not not_26 (not_26_out, I1);
  and and_20 (and_20_out, I3, not_26_out, not_27_out);
  not not_27 (not_27_out, I0);
  not not_28 (not_28_out, I3);
  not not_29 (not_29_out, I1);
  and and_21 (and_21_out, not_28_out, not_29_out, not_30_out);
  not not_30 (not_30_out, I0);
  not not_31 (not_31_out, I3);
  and and_22 (and_22_out, not_31_out, I2, not_32_out);
  not not_32 (not_32_out, I1);
  not not_33 (not_33_out, I3);
  and and_23 (and_23_out, not_33_out, I2, not_34_out);
  not not_34 (not_34_out, I0);
  and and_24 (and_24_out, I3, not_35_out, not_36_out);
  not not_35 (not_35_out, I2);
  not not_36 (not_36_out, I1);
  not not_37 (not_37_out, I2);
  and and_25 (and_25_out, I3, not_37_out, not_38_out);
  not not_38 (not_38_out, I0);
  and and_26 (and_26_out, I3, I2, I1);
  not not_39 (not_39_out, I3);
  not not_40 (not_40_out, I2);
  and and_27 (and_27_out, not_39_out, not_40_out, I1);
  and and_28 (and_28_out, I2, not_41_out);
  not not_41 (not_41_out, I1);
  and and_29 (and_29_out, I2, not_42_out);
  not not_42 (not_42_out, I0);
  and and_30 (and_30_out, I3, not_43_out);
  not not_43 (not_43_out, I1);
  and and_31 (and_31_out, I3, I2);
  or or_1 (A, and_1_out, and_2_out, and_3_out, and_4_out);
  or or_2 (B, not_5_out, and_5_out, and_6_out, and_7_out, and_8_out);
  or or_3 (C, and_9_out, I0, and_10_out, and_11_out);
  or or_4 (E, and_18_out, and_19_out, and_20_out);
  or or_5 (G, and_27_out, and_28_out, and_29_out, and_30_out, and_31_out);
  or or_6 (D, and_12_out, and_13_out, and_14_out, and_15_out, and_16_out, and_17_out);
  or or_7 (F, and_21_out, and_22_out, and_23_out, and_24_out, and_25_out, and_26_out);
endmodule
