// Logisim project main.circ as structural Verilog
module multiplexador (
  input  A,
  input  B,
  input  SELECIONADOR,
  input  \BOTÃO_LIGA ,
  output \SAÍDA 
);

  wire and_1_out, and_2_out, not_1_out;

  not not_1 (not_1_out, SELECIONADOR);
  and and_1 (and_1_out, A, \BOTÃO_LIGA , not_1_out);
  and and_2 (and_2_out, B, \BOTÃO_LIGA , SELECIONADOR);
  or or_1 (\SAÍDA , and_1_out, and_2_out);

  // Notes on the sheet:
  //   E DESLIGA
endmodule

// A
module decodificador (
  input  A3,
  input  A2,
  input  A1,
  input  A0
);

  wire a_1_out_5, b_1_out_5, f_1_out_5, undriven, undriven_2, undriven_3, undriven_4;

  _7_Segment_Display u_7_segment_display_1 (
    .g(undriven), .f(f_1_out_5), .a(a_1_out_5), .b(b_1_out_5), .e(undriven_2), .d(undriven_3), .c(undriven_4));  // open: dp
  a a_1 (.out_5(a_1_out_5), .A3(A3), .A2(A2), .A1(A1), .A0(A0));
  b b_1 (.out_5(b_1_out_5), .A3(A3), .A2(A2), .A1(A1), .A0(A0));
  f f_1 (.out_5(f_1_out_5), .A3(A3), .A2(A2), .A1(A1), .A0(A0));

  // Notes on the sheet:
  //   g
  //   b
  //   a
  //   f
  //   c
  //   d
  //   e
endmodule

module EXEMPLO_DISPLAY (
  input  b,
  input  a,
  input  f,
  input  g,
  input  e,
  input  d,
  input  c
);

  _7_Segment_Display u_7_segment_display_1 (.g(g), .f(f), .a(a), .b(b), .e(e), .d(d), .c(c));  // open: dp
endmodule

module a (
  input  A3,
  input  A2,
  input  A1,
  input  A0,
  output out_5
);

  wire and_1_out, and_2_out, and_3_out, and_4_out, xor_1_out, xor_2_out;

  or or_1 (out_5, and_1_out, and_2_out, and_3_out, and_4_out);
  and and_1 (and_1_out, xor_1_out, xor_2_out);
  and and_2 (and_2_out, A2, A1);
  and and_3 (and_3_out, A3, ~A2, ~A1);  // AND_Gate
  and and_4 (and_4_out, ~A3, ~A2, ~A0);  // AND_Gate
  xor xor_1 (xor_1_out, A0, A3);
  xor xor_2 (xor_2_out, A2, A1);
endmodule

module b (
  input  A3,
  input  A2,
  input  A1,
  input  A0,
  output out_5
);

  wire and_1_out, and_2_out, and_3_out, and_4_out, and_5_out, nand_1_out, or_2_out, xor_1_out;

  or or_1 (out_5, and_1_out, and_2_out, and_3_out, or_2_out);
  and and_1 (and_1_out, A3, A2, ~A1, A0);  // AND_Gate
  and and_2 (and_2_out, nand_1_out, and_4_out);
  and and_3 (and_3_out, xor_1_out, and_5_out);
  or or_2 (or_2_out, ~A3, ~A2);  // OR_Gate
  nand nand_1 (nand_1_out, A1, A0);
  and and_4 (and_4_out, A3, ~A2);  // AND_Gate
  xor xor_1 (xor_1_out, A0, A1);
  and and_5 (and_5_out, A2, ~A3);  // AND_Gate
endmodule

module c (
  input  A3,
  input  A2,
  input  A1,
  input  A0,
  output out_5
);
endmodule

module d (
  input  A3,
  input  A2,
  input  A1,
  input  A0,
  output out_5
);
endmodule

module e (
  input  A3,
  input  A2,
  input  A1,
  input  A0,
  output out_5
);
endmodule

module f (
  input  A3,
  input  A2,
  input  A1,
  input  A0,
  output out_5
);

  wire and_1_out, and_2_out, and_3_out, and_4_out, nand_1_out, nor_1_out;

  or or_1 (out_5, and_1_out, and_2_out, and_3_out, and_4_out);
  and and_1 (and_1_out, A3, A2, A1);
  and and_2 (and_2_out, ~A2, A3);  // AND_Gate
  and and_3 (and_3_out, ~A3, A2, nand_1_out);  // AND_Gate
  and and_4 (and_4_out, ~A3, ~A2, nor_1_out);  // AND_Gate
  nand nand_1 (nand_1_out, A1, A0);
  nor nor_1 (nor_1_out, A1, A0);
endmodule

module g (
  input  A3,
  input  A2,
  input  A1,
  input  A0,
  output out_5
);
endmodule
