// Logisim project portas_com_NAND.circ as structural Verilog
module XOR_3_ENTRADAS (
  input  in_1,
  input  in_2,
  input  in_3,
  input  in_4,
  input  in_5,
  input  in_6,
  output out_7,
  output out_8
);

  wire xor_1_out, xor_com_nand_1_out_3;

  xor xor_1 (xor_1_out, in_1, in_2);
  XOR_COM_NAND xor_com_nand_1 (.in_1(in_4), .in_2(in_5), .out_3(xor_com_nand_1_out_3));
  XOR_COM_NAND xor_com_nand_2 (.in_1(xor_com_nand_1_out_3), .in_2(in_6), .out_3(out_8));
  xor xor_2 (out_7, xor_1_out, in_3);
endmodule

module OR_COM_NAND (
  input  in_1,
  input  in_2,
  output out_3
);

  wire nand_1_out, nand_2_out;

  not nand_1 (nand_1_out, in_1);  // NAND_Gate
  not nand_2 (nand_2_out, in_2);  // NAND_Gate
  nand nand_3 (out_3, nand_1_out, nand_2_out);
endmodule

module AND_COM_NAND (
  input  in_1,
  input  in_2,
  output out_3
);

  wire nand_1_out;

  nand nand_1 (nand_1_out, in_1, in_2);
  nand nand_2 (out_3, nand_1_out, nand_1_out);
endmodule

module NOT_COM_NAND (
  input  in_1,
  output out_2
);

  nand nand_1 (out_2, in_1, in_1);
endmodule

module XOR_COM_NAND (
  input  in_1,
  input  in_2,
  output out_3
);

  wire nand_1_out, nand_2_out, nand_3_out, nand_4_out, nand_5_out, nand_6_out, nand_7_out, nand_8_out;

  nand nand_1 (nand_1_out, in_1, in_1);
  nand nand_2 (nand_2_out, in_2, in_2);
  nand nand_3 (nand_3_out, nand_1_out, in_2);
  nand nand_4 (nand_4_out, in_1, nand_2_out);
  nand nand_5 (nand_5_out, nand_3_out, nand_3_out);
  nand nand_6 (nand_6_out, nand_4_out, nand_4_out);
  not nand_7 (nand_7_out, nand_5_out);  // NAND_Gate
  not nand_8 (nand_8_out, nand_6_out);  // NAND_Gate
  nand nand_9 (out_3, nand_7_out, nand_8_out);
endmodule
