// Logisim project SUM OF SQUARES.circ as structural Verilog: 9 circuits, main circuit main
module main (
  input  [7:0] \Condição_de_Parada ,
  input  [7:0] Incremento
);

  wire button_1_out, clock_1_out;
  wire [3:0] decodificador_1_centenas, decodificador_1_dezenas, decodificador_1_unidades,
       decodificador_2_centenas, decodificador_2_dezenas, decodificador_2_unidades;
  wire [7:0] \sum_1_saída ;

  Clock clock_1 (.out(clock_1_out));
  Button button_1 (.out(button_1_out));
  Hex_Digit_Display hex_digit_display_1 (.value(decodificador_1_centenas));  // open: dp
  Hex_Digit_Display hex_digit_display_2 (.value(decodificador_1_dezenas));  // open: dp
  DECODIFICADOR decodificador_1 (
    .in_1(\Condição_de_Parada ), .CENTENAS(decodificador_1_centenas), .DEZENAS(decodificador_1_dezenas),
    .UNIDADES(decodificador_1_unidades));
  Hex_Digit_Display hex_digit_display_3 (.value(decodificador_1_unidades));  // open: dp
  SUM sum_1 (
    .\Condição_de_Parada (\Condição_de_Parada ), .Incremento(Incremento), .Clock(clock_1_out),
    .Reset(button_1_out), .\Saída (\sum_1_saída ));
  DECODIFICADOR decodificador_2 (
    .in_1(\sum_1_saída ), .CENTENAS(decodificador_2_centenas), .DEZENAS(decodificador_2_dezenas),
    .UNIDADES(decodificador_2_unidades));
  Hex_Digit_Display hex_digit_display_4 (.value(decodificador_2_centenas));  // open: dp
  Hex_Digit_Display hex_digit_display_5 (.value(decodificador_2_dezenas));  // open: dp
  Hex_Digit_Display hex_digit_display_6 (.value(decodificador_2_unidades));  // open: dp
endmodule

// FOR
module FOR___16_bits (
  input  Clock,
  input  Reset,
  input  [15:0] \Condição_de_Parada ,
  input  [15:0] Incremento,
  output [15:0] \Saída ,
  output Ativado
);

  wire comparator_1_lt;
  wire [15:0] adder_1_out;

  Comparator #(.width(16), .mode("unsigned")) comparator_1 (
    .a(\Saída ), .b(\Condição_de_Parada ), .lt(comparator_1_lt));  // open: gt, eq
  Register #(.width(16)) register_1 (.D(adder_1_out), .Q(\Saída ), .clk(Ativado), .clr(Reset));  // open: en
  and and_1 (Ativado, Clock, comparator_1_lt);
  Adder #(.width(16)) adder_1 (.a(\Saída ), .b(Incremento), .out(adder_1_out));  // open: cin, cout
endmodule

// FOR
module FOR___8_bits (
  input  Clock,
  input  Reset,
  input  [7:0] \Condição_de_Parada ,
  input  [7:0] Incremento,
  output [7:0] \Saída ,
  output Ativado
);

  wire comparator_1_lt;
  wire [7:0] adder_1_out;

  Comparator #(.mode("unsigned")) comparator_1 (
    .a(\Saída ), .b(\Condição_de_Parada ), .lt(comparator_1_lt));  // open: gt, eq
  Register register_1 (.D(adder_1_out), .Q(\Saída ), .clk(Ativado), .clr(Reset));  // open: en
  and and_1 (Ativado, Clock, comparator_1_lt);
  Adder adder_1 (.a(\Saída ), .b(Incremento), .out(adder_1_out));  // open: cin, cout
endmodule

// SUM
module SUM_OF_SQUARES (
  input  [7:0] \Condição_de_Parada ,
  input  [7:0] Incremento,
  input  Clock,
  input  Reset,
  output [7:0] \Saída 
);

  wire for_8_bits_1_ativado;
  wire [7:0] adder_1_out, \for_8_bits_1_saída , multiplier_1_out;

  FOR___8_bits for_8_bits_1 (
    .Clock(Clock), .Reset(Reset), .\Condição_de_Parada (\Condição_de_Parada ), .Incremento(Incremento),
    .\Saída (\for_8_bits_1_saída ), .Ativado(for_8_bits_1_ativado));
  Multiplier multiplier_1 (
    .a(\for_8_bits_1_saída ), .b(\for_8_bits_1_saída ), .out(multiplier_1_out));  // open: cin, cout
  Adder adder_1 (.a(\Saída ), .b(multiplier_1_out), .out(adder_1_out));  // open: cin, cout
  Register register_1 (.D(adder_1_out), .Q(\Saída ), .clk(for_8_bits_1_ativado), .clr(Reset));  // open: en
endmodule

module DECODE (
  input  E0,
  input  E1,
  input  E2,
  input  E3,
  input  E4,
  input  E5,
  input  E6,
  input  E7,
  output A0,
  output A1,
  output A2,
  output A3,
  output B0,
  output B1,
  output B2,
  output B3,
  output C0,
  output C1,
  output C2,
  output C3
);

  wire and_1_out, and_2_out, and_3_out, and_4_out, and_5_out, and_6_out, and_7_out, and_8_out, and_9_out,
       and_10_out, and_11_out, and_12_out, and_13_out, and_14_out, and_15_out, and_16_out, and_17_out,
       and_18_out, and_19_out, and_20_out, and_21_out, and_22_out, and_23_out, and_24_out, and_25_out,
       and_26_out, and_27_out, and_28_out, and_29_out, and_30_out, and_31_out, and_32_out, and_33_out,
       and_34_out, and_35_out, and_36_out, and_37_out, and_38_out, and_39_out, and_40_out, and_41_out,
       and_42_out, and_43_out, and_44_out, and_45_out, and_46_out, and_47_out, and_48_out, and_49_out,
       and_50_out, and_51_out, and_52_out, and_53_out, and_54_out, and_55_out, and_56_out, and_57_out,
       and_58_out, and_59_out, and_60_out, and_61_out, and_62_out, and_63_out, and_64_out, and_65_out,
       and_66_out, and_67_out, and_68_out, and_69_out, and_70_out, and_71_out, and_72_out, and_73_out,
       and_74_out, and_75_out, and_76_out, and_77_out, and_78_out, and_79_out, and_80_out, and_81_out,
       and_82_out, and_83_out, and_84_out, and_85_out, and_86_out, and_87_out, and_88_out, and_89_out,
       and_90_out, and_91_out, and_92_out, and_93_out, and_94_out, and_95_out, and_96_out, and_97_out,
       and_98_out, and_99_out, and_100_out, and_101_out, and_102_out, and_103_out, and_104_out, and_105_out,
       and_106_out, and_107_out, and_108_out, and_109_out, and_110_out, and_111_out, and_112_out,
       and_113_out, and_114_out, and_115_out, and_116_out, and_117_out, and_118_out, and_119_out,
       and_120_out, and_121_out, and_122_out, and_123_out, and_124_out, and_125_out, and_126_out,
       and_127_out, and_128_out, and_129_out, and_130_out, and_131_out, and_132_out, and_133_out,
       and_134_out, and_135_out, and_136_out, and_137_out, and_138_out, and_139_out, and_140_out,
       and_141_out, and_142_out, and_143_out, and_144_out, and_145_out, and_146_out, and_147_out,
       and_148_out, and_149_out, and_150_out, and_151_out, and_152_out, and_153_out, and_154_out,
       and_155_out, and_156_out, not_1_out, not_2_out, not_3_out, not_4_out, not_5_out, not_6_out, not_7_out,
       not_8_out, not_9_out, not_10_out, not_11_out, not_12_out, not_13_out, not_14_out, not_15_out,
       not_16_out, not_17_out, not_18_out, not_19_out, not_20_out, not_21_out, not_22_out, not_23_out,
       not_24_out, not_25_out, not_26_out, not_27_out, not_28_out, not_29_out, not_30_out, not_31_out,
       not_32_out, not_33_out, not_34_out, not_35_out, not_36_out, not_37_out, not_38_out, not_39_out,
       not_40_out, not_41_out, not_42_out, not_43_out, not_44_out, not_45_out, not_46_out, not_47_out,
       not_48_out, not_49_out, not_50_out, not_51_out, not_52_out, not_53_out, not_54_out, not_55_out,
       not_56_out, not_57_out, not_58_out, not_59_out, not_60_out, not_61_out, not_62_out, not_63_out,
       not_64_out, not_65_out, not_66_out, not_67_out, not_68_out, not_69_out, not_70_out, not_71_out,
       not_72_out, not_73_out, not_74_out, not_75_out, not_76_out, not_77_out, not_78_out, not_79_out,
       not_80_out, not_81_out, not_82_out, not_83_out, not_84_out, not_85_out, not_86_out, not_87_out,
       not_88_out, not_89_out, not_90_out, not_91_out, not_92_out, not_93_out, not_94_out, not_95_out,
       not_96_out, not_97_out, not_98_out, not_99_out, not_100_out, not_101_out, not_102_out, not_103_out,
       not_104_out, not_105_out, not_106_out, not_107_out, not_108_out, not_109_out, not_110_out,
       not_111_out, not_112_out, not_113_out, not_114_out, not_115_out, not_116_out, not_117_out,
       not_118_out, not_119_out, not_120_out, not_121_out, not_122_out, not_123_out, not_124_out,
       not_125_out, not_126_out, not_127_out, not_128_out, not_129_out, not_130_out, not_131_out,
       not_132_out, not_133_out, not_134_out, not_135_out, not_136_out, not_137_out, not_138_out,
       not_139_out, not_140_out, not_141_out, not_142_out, not_143_out, not_144_out, not_145_out,
       not_146_out, not_147_out, not_148_out, not_149_out, not_150_out, not_151_out, not_152_out,
       not_153_out, not_154_out, not_155_out, not_156_out, not_157_out, not_158_out, not_159_out,
       not_160_out, not_161_out, not_162_out, not_163_out, not_164_out, not_165_out, not_166_out,
       not_167_out, not_168_out, not_169_out, not_170_out, not_171_out, not_172_out, not_173_out,
       not_174_out, not_175_out, not_176_out, not_177_out, not_178_out, not_179_out, not_180_out,
       not_181_out, not_182_out, not_183_out, not_184_out, not_185_out, not_186_out, not_187_out,
       not_188_out, not_189_out, not_190_out, not_191_out, not_192_out, not_193_out, not_194_out,
       not_195_out, not_196_out, not_197_out, not_198_out, not_199_out, not_200_out, not_201_out,
       not_202_out, not_203_out, not_204_out, not_205_out, not_206_out, not_207_out, not_208_out,
       not_209_out, not_210_out, not_211_out, not_212_out, not_213_out, not_214_out, not_215_out,
       not_216_out, not_217_out, not_218_out, not_219_out, not_220_out, not_221_out, not_222_out,
       not_223_out, not_224_out, not_225_out, not_226_out, not_227_out, not_228_out, not_229_out,
       not_230_out, not_231_out, not_232_out, not_233_out, not_234_out, not_235_out, not_236_out,
       not_237_out, not_238_out, not_239_out, not_240_out, not_241_out, not_242_out, not_243_out,
       not_244_out, not_245_out, not_246_out, not_247_out, not_248_out, not_249_out, not_250_out,
       not_251_out, not_252_out, not_253_out, not_254_out, not_255_out, not_256_out, not_257_out,
       not_258_out, not_259_out, not_260_out, not_261_out, not_262_out, not_263_out, not_264_out,
       not_265_out, not_266_out, not_267_out, not_268_out, not_269_out, not_270_out, not_271_out,
       not_272_out, not_273_out, not_274_out, not_275_out, not_276_out, not_277_out, not_278_out,
       not_279_out, not_280_out, not_281_out, not_282_out, not_283_out, not_284_out, not_285_out,
       not_286_out, not_287_out, not_288_out, not_289_out, not_290_out, not_291_out, not_292_out,
       not_293_out, not_294_out, not_295_out, not_296_out, not_297_out, not_298_out, not_299_out,
       not_300_out, not_301_out, not_302_out, not_303_out, not_304_out, not_305_out, not_306_out,
       not_307_out, not_308_out, not_309_out, not_310_out, not_311_out, not_312_out, not_313_out,
       not_314_out, not_315_out, not_316_out, not_317_out, not_318_out, not_319_out, not_320_out,
       not_321_out, not_322_out, not_323_out, not_324_out, not_325_out, not_326_out, not_327_out,
       not_328_out, not_329_out, not_330_out, not_331_out, not_332_out, not_333_out, not_334_out,
       not_335_out, not_336_out, not_337_out, not_338_out, not_339_out, not_340_out, not_341_out,
       not_342_out, not_343_out, not_344_out, not_345_out, not_346_out, not_347_out, not_348_out,
       not_349_out, not_350_out, not_351_out, not_352_out, not_353_out, not_354_out, not_355_out,
       not_356_out, not_357_out, not_358_out, not_359_out, not_360_out, not_361_out, not_362_out,
       not_363_out, not_364_out, not_365_out, not_366_out, not_367_out, not_368_out, not_369_out,
       not_370_out, not_371_out, not_372_out, not_373_out, not_374_out, not_375_out, not_376_out,
       not_377_out, not_378_out, not_379_out, not_380_out, not_381_out, not_382_out, not_383_out,
       not_384_out, not_385_out, not_386_out, not_387_out, not_388_out, not_389_out, not_390_out,
       not_391_out, not_392_out, not_393_out, not_394_out, not_395_out, not_396_out, not_397_out,
       not_398_out, not_399_out, not_400_out, not_401_out, not_402_out, not_403_out, not_404_out,
       not_405_out, not_406_out, not_407_out, not_408_out, not_409_out, not_410_out, not_411_out,
       not_412_out, not_413_out, not_414_out, not_415_out, not_416_out, not_417_out, not_418_out,
       not_419_out, not_420_out, not_421_out, not_422_out, not_423_out, not_424_out, not_425_out,
       not_426_out, not_427_out, or_6_out, or_7_out, or_8_out, or_9_out;

  and and_1 (and_1_out, E0, E1, E4);
  and and_2 (and_2_out, E0, E1, E3);
  and and_3 (and_3_out, E0, E1, E2);
  not not_1 (not_1_out, E0);
  not not_2 (not_2_out, E0);
  not not_3 (not_3_out, E0);
  not not_4 (not_4_out, E1);
  not not_5 (not_5_out, E2);
  not not_6 (not_6_out, E3);
  not not_7 (not_7_out, E4);
  not not_8 (not_8_out, E0);
  not not_9 (not_9_out, E2);
  not not_10 (not_10_out, E0);
  not not_11 (not_11_out, E3);
  not not_12 (not_12_out, E4);
  not not_13 (not_13_out, E5);
  not not_14 (not_14_out, E1);
  not not_15 (not_15_out, E1);
  not not_16 (not_16_out, E2);
  not not_17 (not_17_out, E3);
  not not_18 (not_18_out, E4);
  not not_19 (not_19_out, E1);
  not not_20 (not_20_out, E3);
  not not_21 (not_21_out, E0);
  not not_22 (not_22_out, E1);
  not not_23 (not_23_out, E0);
  not not_24 (not_24_out, E2);
  not not_25 (not_25_out, E3);
  not not_26 (not_26_out, E1);
  not not_27 (not_27_out, E3);
  not not_28 (not_28_out, E1);
  not not_29 (not_29_out, E2);
  not not_30 (not_30_out, E1);
  not not_31 (not_31_out, E3);
  not not_32 (not_32_out, E1);
  not not_33 (not_33_out, E4);
  not not_34 (not_34_out, E5);
  not not_35 (not_35_out, E0);
  not not_36 (not_36_out, E1);
  not not_37 (not_37_out, E2);
  not not_38 (not_38_out, E0);
  not not_39 (not_39_out, E1);
  not not_40 (not_40_out, E2);
  not not_41 (not_41_out, E0);
  not not_42 (not_42_out, E1);
  not not_43 (not_43_out, E1);
  not not_44 (not_44_out, E3);
  not not_45 (not_45_out, E4);
  not not_46 (not_46_out, E0);
  not not_47 (not_47_out, E2);
  not not_48 (not_48_out, E3);
  not not_49 (not_49_out, E0);
  not not_50 (not_50_out, E1);
  not not_51 (not_51_out, E3);
  not not_52 (not_52_out, E4);
  not not_53 (not_53_out, E1);
  not not_54 (not_54_out, E3);
  not not_55 (not_55_out, E5);
  not not_56 (not_56_out, E1);
  not not_57 (not_57_out, E4);
  not not_58 (not_58_out, E5);
  not not_59 (not_59_out, E3);
  not not_60 (not_60_out, E2);
  not not_61 (not_61_out, E0);
  not not_62 (not_62_out, E2);
  not not_63 (not_63_out, E3);
  not not_64 (not_64_out, E0);
  not not_65 (not_65_out, E2);
  not not_66 (not_66_out, E3);
  not not_67 (not_67_out, E0);
  not not_68 (not_68_out, E2);
  not not_69 (not_69_out, E0);
  not not_70 (not_70_out, E1);
  not not_71 (not_71_out, E2);
  not not_72 (not_72_out, E4);
  not not_73 (not_73_out, E5);
  not not_74 (not_74_out, E0);
  not not_75 (not_75_out, E1);
  not not_76 (not_76_out, E3);
  not not_77 (not_77_out, E4);
  not not_78 (not_78_out, E0);
  not not_79 (not_79_out, E1);
  not not_80 (not_80_out, E4);
  not not_81 (not_81_out, E0);
  not not_82 (not_82_out, E4);
  not not_83 (not_83_out, E0);
  not not_84 (not_84_out, E1);
  not not_85 (not_85_out, E5);
  not not_86 (not_86_out, E2);
  not not_87 (not_87_out, E3);
  not not_88 (not_88_out, E4);
  not not_89 (not_89_out, E0);
  not not_90 (not_90_out, E2);
  not not_91 (not_91_out, E3);
  not not_92 (not_92_out, E0);
  not not_93 (not_93_out, E2);
  not not_94 (not_94_out, E0);
  not not_95 (not_95_out, E2);
  not not_96 (not_96_out, E0);
  not not_97 (not_97_out, E3);
  not not_98 (not_98_out, E0);
  not not_99 (not_99_out, E4);
  not not_100 (not_100_out, E5);
  not not_101 (not_101_out, E2);
  not not_102 (not_102_out, E3);
  not not_103 (not_103_out, E4);
  not not_104 (not_104_out, E2);
  not not_105 (not_105_out, E3);
  not not_106 (not_106_out, E4);
  not not_107 (not_107_out, E2);
  not not_108 (not_108_out, E4);
  not not_109 (not_109_out, E1);
  not not_110 (not_110_out, E2);
  not not_111 (not_111_out, E5);
  not not_112 (not_112_out, E1);
  not not_113 (not_113_out, E2);
  not not_114 (not_114_out, E2);
  not not_115 (not_115_out, E5);
  not not_116 (not_116_out, E3);
  not not_117 (not_117_out, E3);
  not not_118 (not_118_out, E1);
  not not_119 (not_119_out, E4);
  not not_120 (not_120_out, E5);
  not not_121 (not_121_out, E2);
  not not_122 (not_122_out, E3);
  not not_123 (not_123_out, E4);
  not not_124 (not_124_out, E2);
  not not_125 (not_125_out, E4);
  not not_126 (not_126_out, E2);
  not not_127 (not_127_out, E4);
  not not_128 (not_128_out, E3);
  not not_129 (not_129_out, E4);
  not not_130 (not_130_out, E3);
  not not_131 (not_131_out, E0);
  not not_132 (not_132_out, E1);
  not not_133 (not_133_out, E2);
  not not_134 (not_134_out, E3);
  not not_135 (not_135_out, E5);
  not not_136 (not_136_out, E6);
  not not_137 (not_137_out, E0);
  not not_138 (not_138_out, E1);
  not not_139 (not_139_out, E2);
  not not_140 (not_140_out, E4);
  not not_141 (not_141_out, E5);
  not not_142 (not_142_out, E0);
  not not_143 (not_143_out, E1);
  not not_144 (not_144_out, E2);
  not not_145 (not_145_out, E6);
  not not_146 (not_146_out, E0);
  not not_147 (not_147_out, E1);
  not not_148 (not_148_out, E3);
  not not_149 (not_149_out, E4);
  not not_150 (not_150_out, E0);
  not not_151 (not_151_out, E1);
  not not_152 (not_152_out, E4);
  not not_153 (not_153_out, E5);
  not not_154 (not_154_out, E6);
  not not_155 (not_155_out, E0);
  not not_156 (not_156_out, E1);
  not not_157 (not_157_out, E5);
  not not_158 (not_158_out, E0);
  not not_159 (not_159_out, E2);
  not not_160 (not_160_out, E3);
  not not_161 (not_161_out, E4);
  not not_162 (not_162_out, E6);
  not not_163 (not_163_out, E0);
  not not_164 (not_164_out, E2);
  not not_165 (not_165_out, E3);
  not not_166 (not_166_out, E0);
  not not_167 (not_167_out, E2);
  not not_168 (not_168_out, E5);
  not not_169 (not_169_out, E6);
  not not_170 (not_170_out, E0);
  not not_171 (not_171_out, E3);
  not not_172 (not_172_out, E4);
  not not_173 (not_173_out, E5);
  not not_174 (not_174_out, E0);
  not not_175 (not_175_out, E3);
  not not_176 (not_176_out, E6);
  not not_177 (not_177_out, E0);
  not not_178 (not_178_out, E4);
  not not_179 (not_179_out, E1);
  not not_180 (not_180_out, E2);
  not not_181 (not_181_out, E3);
  not not_182 (not_182_out, E4);
  not not_183 (not_183_out, E5);
  not not_184 (not_184_out, E6);
  not not_185 (not_185_out, E1);
  not not_186 (not_186_out, E2);
  not not_187 (not_187_out, E3);
  not not_188 (not_188_out, E5);
  not not_189 (not_189_out, E1);
  not not_190 (not_190_out, E2);
  not not_191 (not_191_out, E4);
  not not_192 (not_192_out, E6);
  not not_193 (not_193_out, E1);
  not not_194 (not_194_out, E2);
  not not_195 (not_195_out, E1);
  not not_196 (not_196_out, E3);
  not not_197 (not_197_out, E5);
  not not_198 (not_198_out, E6);
  not not_199 (not_199_out, E1);
  not not_200 (not_200_out, E4);
  not not_201 (not_201_out, E5);
  not not_202 (not_202_out, E1);
  not not_203 (not_203_out, E6);
  not not_204 (not_204_out, E2);
  not not_205 (not_205_out, E3);
  not not_206 (not_206_out, E4);
  not not_207 (not_207_out, E2);
  not not_208 (not_208_out, E4);
  not not_209 (not_209_out, E5);
  not not_210 (not_210_out, E6);
  not not_211 (not_211_out, E2);
  not not_212 (not_212_out, E5);
  not not_213 (not_213_out, E3);
  not not_214 (not_214_out, E4);
  not not_215 (not_215_out, E6);
  not not_216 (not_216_out, E3);
  not not_217 (not_217_out, E5);
  not not_218 (not_218_out, E6);
  not not_219 (not_219_out, E0);
  not not_220 (not_220_out, E1);
  not not_221 (not_221_out, E2);
  not not_222 (not_222_out, E3);
  not not_223 (not_223_out, E4);
  not not_224 (not_224_out, E0);
  not not_225 (not_225_out, E1);
  not not_226 (not_226_out, E2);
  not not_227 (not_227_out, E3);
  not not_228 (not_228_out, E1);
  not not_229 (not_229_out, E2);
  not not_230 (not_230_out, E4);
  not not_231 (not_231_out, E5);
  not not_232 (not_232_out, E6);
  not not_233 (not_233_out, E0);
  not not_234 (not_234_out, E1);
  not not_235 (not_235_out, E2);
  not not_236 (not_236_out, E5);
  not not_237 (not_237_out, E0);
  not not_238 (not_238_out, E1);
  not not_239 (not_239_out, E5);
  not not_240 (not_240_out, E6);
  not not_241 (not_241_out, E0);
  not not_242 (not_242_out, E1);
  not not_243 (not_243_out, E3);
  not not_244 (not_244_out, E4);
  not not_245 (not_245_out, E5);
  not not_246 (not_246_out, E1);
  not not_247 (not_247_out, E3);
  not not_248 (not_248_out, E4);
  not not_249 (not_249_out, E6);
  not not_250 (not_250_out, E0);
  not not_251 (not_251_out, E1);
  not not_252 (not_252_out, E3);
  not not_253 (not_253_out, E0);
  not not_254 (not_254_out, E1);
  not not_255 (not_255_out, E4);
  not not_256 (not_256_out, E0);
  not not_257 (not_257_out, E2);
  not not_258 (not_258_out, E3);
  not not_259 (not_259_out, E4);
  not not_260 (not_260_out, E5);
  not not_261 (not_261_out, E0);
  not not_262 (not_262_out, E2);
  not not_263 (not_263_out, E3);
  not not_264 (not_264_out, E5);
  not not_265 (not_265_out, E2);
  not not_266 (not_266_out, E3);
  not not_267 (not_267_out, E6);
  not not_268 (not_268_out, E0);
  not not_269 (not_269_out, E2);
  not not_270 (not_270_out, E4);
  not not_271 (not_271_out, E0);
  not not_272 (not_272_out, E2);
  not not_273 (not_273_out, E3);
  not not_274 (not_274_out, E4);
  not not_275 (not_275_out, E5);
  not not_276 (not_276_out, E6);
  not not_277 (not_277_out, E0);
  not not_278 (not_278_out, E3);
  not not_279 (not_279_out, E5);
  not not_280 (not_280_out, E0);
  not not_281 (not_281_out, E4);
  not not_282 (not_282_out, E5);
  not not_283 (not_283_out, E4);
  not not_284 (not_284_out, E6);
  not not_285 (not_285_out, E0);
  not not_286 (not_286_out, E1);
  not not_287 (not_287_out, E3);
  not not_288 (not_288_out, E4);
  not not_289 (not_289_out, E1);
  not not_290 (not_290_out, E2);
  not not_291 (not_291_out, E3);
  not not_292 (not_292_out, E5);
  not not_293 (not_293_out, E6);
  not not_294 (not_294_out, E1);
  not not_295 (not_295_out, E2);
  not not_296 (not_296_out, E5);
  not not_297 (not_297_out, E1);
  not not_298 (not_298_out, E2);
  not not_299 (not_299_out, E6);
  not not_300 (not_300_out, E1);
  not not_301 (not_301_out, E3);
  not not_302 (not_302_out, E1);
  not not_303 (not_303_out, E5);
  not not_304 (not_304_out, E6);
  not not_305 (not_305_out, E1);
  not not_306 (not_306_out, E5);
  not not_307 (not_307_out, E3);
  not not_308 (not_308_out, E4);
  not not_309 (not_309_out, E5);
  not not_310 (not_310_out, E2);
  not not_311 (not_311_out, E3);
  not not_312 (not_312_out, E6);
  not not_313 (not_313_out, E2);
  not not_314 (not_314_out, E3);
  not not_315 (not_315_out, E3);
  not not_316 (not_316_out, E6);
  not not_317 (not_317_out, E4);
  not not_318 (not_318_out, E2);
  not not_319 (not_319_out, E5);
  not not_320 (not_320_out, E6);
  not not_321 (not_321_out, E3);
  not not_322 (not_322_out, E5);
  not not_323 (not_323_out, E0);
  not not_324 (not_324_out, E2);
  not not_325 (not_325_out, E3);
  not not_326 (not_326_out, E4);
  not not_327 (not_327_out, E5);
  not not_328 (not_328_out, E0);
  not not_329 (not_329_out, E1);
  not not_330 (not_330_out, E2);
  not not_331 (not_331_out, E4);
  not not_332 (not_332_out, E0);
  not not_333 (not_333_out, E2);
  not not_334 (not_334_out, E3);
  not not_335 (not_335_out, E6);
  not not_336 (not_336_out, E0);
  not not_337 (not_337_out, E1);
  not not_338 (not_338_out, E2);
  not not_339 (not_339_out, E4);
  not not_340 (not_340_out, E5);
  not not_341 (not_341_out, E6);
  not not_342 (not_342_out, E0);
  not not_343 (not_343_out, E1);
  not not_344 (not_344_out, E2);
  not not_345 (not_345_out, E5);
  not not_346 (not_346_out, E0);
  not not_347 (not_347_out, E3);
  not not_348 (not_348_out, E4);
  not not_349 (not_349_out, E5);
  not not_350 (not_350_out, E6);
  not not_351 (not_351_out, E0);
  not not_352 (not_352_out, E1);
  not not_353 (not_353_out, E4);
  not not_354 (not_354_out, E6);
  not not_355 (not_355_out, E0);
  not not_356 (not_356_out, E3);
  not not_357 (not_357_out, E5);
  not not_358 (not_358_out, E0);
  not not_359 (not_359_out, E1);
  not not_360 (not_360_out, E0);
  not not_361 (not_361_out, E1);
  not not_362 (not_362_out, E5);
  not not_363 (not_363_out, E6);
  not not_364 (not_364_out, E0);
  not not_365 (not_365_out, E2);
  not not_366 (not_366_out, E3);
  not not_367 (not_367_out, E6);
  not not_368 (not_368_out, E0);
  not not_369 (not_369_out, E2);
  not not_370 (not_370_out, E6);
  not not_371 (not_371_out, E0);
  not not_372 (not_372_out, E2);
  not not_373 (not_373_out, E4);
  not not_374 (not_374_out, E0);
  not not_375 (not_375_out, E3);
  not not_376 (not_376_out, E4);
  not not_377 (not_377_out, E0);
  not not_378 (not_378_out, E4);
  not not_379 (not_379_out, E6);
  not not_380 (not_380_out, E0);
  not not_381 (not_381_out, E2);
  not not_382 (not_382_out, E3);
  not not_383 (not_383_out, E4);
  not not_384 (not_384_out, E6);
  not not_385 (not_385_out, E1);
  not not_386 (not_386_out, E2);
  not not_387 (not_387_out, E5);
  not not_388 (not_388_out, E6);
  not not_389 (not_389_out, E2);
  not not_390 (not_390_out, E3);
  not not_391 (not_391_out, E1);
  not not_392 (not_392_out, E2);
  not not_393 (not_393_out, E4);
  not not_394 (not_394_out, E5);
  not not_395 (not_395_out, E1);
  not not_396 (not_396_out, E2);
  not not_397 (not_397_out, E6);
  not not_398 (not_398_out, E2);
  not not_399 (not_399_out, E5);
  not not_400 (not_400_out, E6);
  not not_401 (not_401_out, E3);
  not not_402 (not_402_out, E4);
  not not_403 (not_403_out, E5);
  not not_404 (not_404_out, E1);
  not not_405 (not_405_out, E4);
  not not_406 (not_406_out, E3);
  not not_407 (not_407_out, E6);
  not not_408 (not_408_out, E1);
  not not_409 (not_409_out, E4);
  not not_410 (not_410_out, E5);
  not not_411 (not_411_out, E6);
  not not_412 (not_412_out, E1);
  not not_413 (not_413_out, E5);
  not not_414 (not_414_out, E2);
  not not_415 (not_415_out, E3);
  not not_416 (not_416_out, E4);
  not not_417 (not_417_out, E6);
  not not_418 (not_418_out, E2);
  not not_419 (not_419_out, E4);
  not not_420 (not_420_out, E6);
  not not_421 (not_421_out, E2);
  not not_422 (not_422_out, E3);
  not not_423 (not_423_out, E2);
  not not_424 (not_424_out, E3);
  not not_425 (not_425_out, E6);
  not not_426 (not_426_out, E6);
  not not_427 (not_427_out, E4);
  or or_1 (A2, and_1_out, and_2_out, and_3_out);
  and and_4 (and_4_out, not_1_out, E1, E2, E5);
  and and_5 (and_5_out, not_2_out, E1, E2, E4);
  and and_6 (and_6_out, not_3_out, E1, E2, E3);
  and and_7 (and_7_out, E0, not_4_out);
  and and_8 (and_8_out, E0, not_5_out, not_6_out, not_7_out);
  and and_9 (and_9_out, not_8_out, E1, not_9_out, E3);
  and and_10 (and_10_out, not_10_out, E1, E2, not_11_out, not_12_out, not_13_out);
  and and_11 (and_11_out, E0, not_14_out, E2, E3, E5);
  and and_12 (and_12_out, E0, not_15_out, E2, E3, E4);
  and and_13 (and_13_out, E0, E1, not_16_out, not_17_out, not_18_out);
  and and_14 (and_14_out, not_19_out, E2, not_20_out, E4);
  and and_15 (and_15_out, not_21_out, not_22_out, E2, E3);
  and and_16 (and_16_out, not_23_out, E1, not_24_out, not_25_out);
  and and_17 (and_17_out, E0, not_26_out, not_27_out, E4, E5);
  and and_18 (and_18_out, E0, not_28_out, not_29_out, E3);
  and and_19 (and_19_out, E0, not_30_out, E2, not_31_out);
  and and_20 (and_20_out, E0, not_32_out, E2, not_33_out, not_34_out);
  and and_21 (and_21_out, E0, E1, E2, E3);
  and and_22 (and_22_out, not_35_out, not_36_out, not_37_out, E3, E5);
  and and_23 (and_23_out, not_38_out, not_39_out, not_40_out, E3, E4);
  and and_24 (and_24_out, not_41_out, not_42_out, E3, E4, E5);
  and and_25 (and_25_out, not_43_out, E2, not_44_out, not_45_out);
  and and_26 (and_26_out, not_46_out, E1, not_47_out, not_48_out);
  and and_27 (and_27_out, not_49_out, E1, E2, E3, E4);
  and and_28 (and_28_out, E0, not_50_out, not_51_out, not_52_out);
  and and_29 (and_29_out, E0, not_53_out, not_54_out, not_55_out);
  and and_30 (and_30_out, E0, not_56_out, E2, not_57_out, not_58_out);
  and and_31 (and_31_out, E0, E2, not_59_out);
  and and_32 (and_32_out, E0, E1, not_60_out, E3, E4, E5);
  and and_33 (and_33_out, not_61_out, not_62_out, not_63_out, E4, E6);
  and and_34 (and_34_out, not_64_out, not_65_out, not_66_out, E4, E5);
  and and_35 (and_35_out, not_67_out, not_68_out, E4, E5, E6);
  and and_36 (and_36_out, not_69_out, not_70_out, not_71_out, E3, not_72_out, not_73_out);
  and and_37 (and_37_out, not_74_out, not_75_out, E2, not_76_out, not_77_out);
  and and_38 (and_38_out, not_78_out, not_79_out, E2, not_80_out, E6);
  and and_39 (and_39_out, not_81_out, E2, E3, not_82_out, E5);
  and and_40 (and_40_out, not_83_out, not_84_out, E2, E3, E4, not_85_out);
  and and_41 (and_41_out, E1, not_86_out, not_87_out, not_88_out, E5, E6);
  and and_42 (and_42_out, not_89_out, E1, not_90_out, not_91_out, E4);
  and and_43 (and_43_out, not_92_out, E1, not_93_out, E4, E6);
  and and_44 (and_44_out, not_94_out, E1, not_95_out, E4, E5);
  and and_45 (and_45_out, not_96_out, E1, not_97_out, E4, E5, E6);
  and and_46 (and_46_out, not_98_out, E1, E2, not_99_out, not_100_out);
  and and_47 (and_47_out, E0, not_101_out, not_102_out, not_103_out, E6);
  and and_48 (and_48_out, E0, not_104_out, not_105_out, not_106_out, E5);
  and and_49 (and_49_out, E0, not_107_out, not_108_out, E5, E6);
  and and_50 (and_50_out, E0, not_109_out, not_110_out, E4, not_111_out);
  and and_51 (and_51_out, E0, not_112_out, not_113_out, E3, E4);
  and and_52 (and_52_out, E0, not_114_out, E3, E4, not_115_out);
  and and_53 (and_53_out, E0, E2, not_116_out, E4, E6);
  and and_54 (and_54_out, E0, E2, not_117_out, E4, E5);
  and and_55 (and_55_out, E0, E2, E4, E5, E6);
  and and_56 (and_56_out, E0, not_118_out, E2, E3, not_119_out, not_120_out);
  and and_57 (and_57_out, E0, E1, not_121_out, not_122_out, not_123_out);
  and and_58 (and_58_out, E0, E1, not_124_out, not_125_out, E6);
  and and_59 (and_59_out, E0, E1, not_126_out, not_127_out, E5);
  and and_60 (and_60_out, E0, E1, not_128_out, not_129_out, E5, E6);
  and and_61 (and_61_out, E0, E1, E2, not_130_out, E4);
  and and_62 (and_62_out, E0, E1, E2, E4, E6);
  and and_63 (and_63_out, E0, E1, E2, E4, E5);
  and and_64 (and_64_out, not_131_out, not_132_out, not_133_out, not_134_out, E4, not_135_out, not_136_out);
  and and_65 (and_65_out, not_137_out, not_138_out, not_139_out, E3, not_140_out, not_141_out, E6);
  and and_66 (and_66_out, not_142_out, not_143_out, not_144_out, E3, E4, E5, not_145_out);
  and and_67 (and_67_out, not_146_out, not_147_out, E2, not_148_out, not_149_out, E5, E6);
  and and_68 (and_68_out, not_150_out, not_151_out, E2, E3, not_152_out, not_153_out, not_154_out);
  and and_69 (and_69_out, not_155_out, not_156_out, E2, E3, E4, not_157_out, E6);
  and and_70 (and_70_out, not_158_out, E1, not_159_out, not_160_out, not_161_out, E5, not_162_out);
  and and_71 (and_71_out, not_163_out, E1, not_164_out, not_165_out, E4, E5, E6);
  and and_72 (and_72_out, not_166_out, E1, not_167_out, E3, E4, not_168_out, not_169_out);
  and and_73 (and_73_out, not_170_out, E1, E2, not_171_out, not_172_out, not_173_out, E6);
  and and_74 (and_74_out, not_174_out, E1, E2, not_175_out, E4, E5, not_176_out);
  and and_75 (and_75_out, not_177_out, E1, E2, E3, not_178_out, E5, E6);
  and and_76 (and_76_out, E0, not_179_out, not_180_out, not_181_out, not_182_out, not_183_out, not_184_out);
  and and_77 (and_77_out, E0, not_185_out, not_186_out, not_187_out, E4, not_188_out, E6);
  and and_78 (and_78_out, E0, not_189_out, not_190_out, E3, not_191_out, E5, not_192_out);
  and and_79 (and_79_out, E0, not_193_out, not_194_out, E3, E4, E5, E6);
  and and_80 (and_80_out, E0, not_195_out, E2, not_196_out, E4, not_197_out, not_198_out);
  and and_81 (and_81_out, E0, not_199_out, E2, E3, not_200_out, not_201_out, E6);
  and and_82 (and_82_out, E0, not_202_out, E2, E3, E4, E5, not_203_out);
  and and_83 (and_83_out, E0, E1, not_204_out, not_205_out, not_206_out, E5, E6);
  and and_84 (and_84_out, E0, E1, not_207_out, E3, not_208_out, not_209_out, not_210_out);
  and and_85 (and_85_out, E0, E1, not_211_out, E3, E4, not_212_out, E6);
  and and_86 (and_86_out, E0, E1, E2, not_213_out, not_214_out, E5, not_215_out);
  and and_87 (and_87_out, E0, E1, E2, not_216_out, E4, E5, E6);
  and and_88 (and_88_out, E0, E1, E2, E3, E4, not_217_out, not_218_out);
  and and_89 (and_89_out, not_219_out, not_220_out, not_221_out, not_222_out, not_223_out, E5);
  and and_90 (and_90_out, not_224_out, not_225_out, not_226_out, not_227_out, E5, E6);
  and and_91 (and_91_out, not_228_out, not_229_out, E3, not_230_out, not_231_out, not_232_out);
  and and_92 (and_92_out, not_233_out, not_234_out, not_235_out, E3, E4, not_236_out);
  and and_93 (and_93_out, not_237_out, not_238_out, E3, E4, not_239_out, not_240_out);
  and and_94 (and_94_out, not_241_out, not_242_out, E2, not_243_out, not_244_out, not_245_out, E6);
  and and_95 (and_95_out, not_246_out, E2, not_247_out, not_248_out, E5, not_249_out);
  and and_96 (and_96_out, not_250_out, not_251_out, E2, not_252_out, E4, E5);
  and and_97 (and_97_out, not_253_out, not_254_out, E2, E3, not_255_out, E5, E6);
  and and_98 (and_98_out, not_256_out, E1, not_257_out, not_258_out, not_259_out, not_260_out);
  and and_99 (and_99_out, not_261_out, E1, not_262_out, not_263_out, not_264_out, E6);
  and and_100 (and_100_out, E1, not_265_out, not_266_out, E4, E5, not_267_out);
  and and_101 (and_101_out, not_268_out, E1, not_269_out, E3, not_270_out, E5);
  and and_102 (and_102_out, not_271_out, E1, not_272_out, E3, E5, E6);
  and and_103 (and_103_out, E1, E2, not_273_out, not_274_out, not_275_out, not_276_out);
  and and_104 (and_104_out, not_277_out, E1, E2, not_278_out, E4, not_279_out);
  and and_105 (and_105_out, not_280_out, E1, E2, E3, not_281_out, not_282_out, E6);
  and and_106 (and_106_out, E1, E2, E3, not_283_out, E5, not_284_out);
  and and_107 (and_107_out, not_285_out, E1, E2, E3, E4, E5);
  and and_108 (and_108_out, E0, not_286_out, not_287_out, not_288_out, E5, E6);
  and and_109 (and_109_out, E0, not_289_out, not_290_out, not_291_out, E4, not_292_out, not_293_out);
  and and_110 (and_110_out, E0, not_294_out, not_295_out, E3, not_296_out, E6);
  and and_111 (and_111_out, E0, not_297_out, not_298_out, E3, E4, E5, not_299_out);
  and and_112 (and_112_out, E0, not_300_out, E2, not_301_out, E5, E6);
  and and_113 (and_113_out, E0, not_302_out, E2, E3, not_303_out, not_304_out);
  and and_114 (and_114_out, E0, not_305_out, E2, E3, E4, not_306_out);
  and and_115 (and_115_out, E0, E1, not_307_out, not_308_out, not_309_out, E6);
  and and_116 (and_116_out, E0, E1, not_310_out, not_311_out, E5, not_312_out);
  and and_117 (and_117_out, E0, E1, not_313_out, not_314_out, E4, E5);
  and and_118 (and_118_out, E0, E1, not_315_out, E4, E5, not_316_out);
  and and_119 (and_119_out, E0, E1, E3, not_317_out, E5, E6);
  and and_120 (and_120_out, E0, E1, not_318_out, E3, E4, not_319_out, not_320_out);
  and and_121 (and_121_out, E0, E1, E2, not_321_out, not_322_out, E6);
  and and_122 (and_122_out, E0, E1, E2, E3, E5, E6);
  and and_123 (and_123_out, not_323_out, not_324_out, not_325_out, not_326_out, not_327_out, E6);
  and and_124 (and_124_out, not_328_out, not_329_out, not_330_out, not_331_out, E5, E6);
  and and_125 (and_125_out, not_332_out, not_333_out, not_334_out, E4, E5, not_335_out);
  and and_126 (and_126_out, not_336_out, not_337_out, not_338_out, E3, not_339_out, not_340_out, not_341_out);
  and and_127 (and_127_out, not_342_out, not_343_out, not_344_out, E3, E4, not_345_out, E6);
  and and_128 (and_128_out, not_346_out, E2, not_347_out, not_348_out, not_349_out, not_350_out);
  and and_129 (and_129_out, not_351_out, not_352_out, E2, not_353_out, E5, not_354_out);
  and and_130 (and_130_out, not_355_out, E2, not_356_out, E4, not_357_out, E6);
  and and_131 (and_131_out, not_358_out, not_359_out, E2, E4, E5, E6);
  and and_132 (and_132_out, not_360_out, not_361_out, E2, E3, E4, not_362_out, not_363_out);
  and and_133 (and_133_out, not_364_out, E1, not_365_out, not_366_out, E4, not_367_out);
  and and_134 (and_134_out, not_368_out, E1, not_369_out, E4, E5, not_370_out);
  and and_135 (and_135_out, not_371_out, E1, not_372_out, E3, not_373_out, E6);
  and and_136 (and_136_out, not_374_out, E1, E2, not_375_out, not_376_out, E5, E6);
  and and_137 (and_137_out, not_377_out, E1, E2, E3, not_378_out, not_379_out);
  and and_138 (and_138_out, not_380_out, E1, E2, E3, E4, E6);
  and and_139 (and_139_out, E0, not_381_out, not_382_out, not_383_out, E5, not_384_out);
  and and_140 (and_140_out, E0, not_385_out, not_386_out, E4, not_387_out, not_388_out);
  and and_141 (and_141_out, E0, not_389_out, not_390_out, E4, E5, E6);
  and and_142 (and_142_out, E0, not_391_out, not_392_out, E3, not_393_out, not_394_out, E6);
  and and_143 (and_143_out, E0, not_395_out, not_396_out, E3, E4, not_397_out);
  and and_144 (and_144_out, E0, not_398_out, E3, E4, not_399_out, not_400_out);
  and and_145 (and_145_out, E0, E2, not_401_out, not_402_out, not_403_out, E6);
  and and_146 (and_146_out, E0, not_404_out, E2, not_405_out, E5, E6);
  and and_147 (and_147_out, E0, E2, not_406_out, E4, E5, not_407_out);
  and and_148 (and_148_out, E0, not_408_out, E2, E3, not_409_out, not_410_out, not_411_out);
  and and_149 (and_149_out, E0, not_412_out, E2, E3, E4, not_413_out, E6);
  and and_150 (and_150_out, E0, E1, not_414_out, not_415_out, not_416_out, not_417_out);
  and and_151 (and_151_out, E0, E1, not_418_out, not_419_out, E5, not_420_out);
  and and_152 (and_152_out, E0, E1, not_421_out, not_422_out, E4, E6);
  and and_153 (and_153_out, E0, E1, not_423_out, E4, E5, E6);
  and and_154 (and_154_out, E0, E1, E2, not_424_out, E4, not_425_out);
  and and_155 (and_155_out, E0, E1, E2, E4, E5, not_426_out);
  and and_156 (and_156_out, E0, E1, E2, E3, not_427_out, E6);
  or or_2 (A3, and_4_out, and_5_out, and_6_out, and_7_out, and_8_out);
  or or_3 (B0, and_9_out, and_10_out, and_11_out, and_12_out, and_13_out);
  or or_4 (B1, and_14_out, and_15_out, and_16_out, and_17_out, and_18_out, and_19_out, and_20_out, and_21_out);
  or or_5 (B2, and_22_out, and_23_out, and_24_out, and_25_out, and_26_out, and_27_out, and_28_out, and_29_out, and_30_out, and_31_out, and_32_out);
  or or_6 (or_6_out, and_89_out, and_90_out, and_91_out, and_92_out, and_93_out, and_94_out, and_95_out, and_96_out, and_97_out, and_98_out, and_99_out, and_100_out, and_101_out, and_102_out, and_103_out, and_104_out, and_105_out);
  or or_7 (or_7_out, and_106_out, and_107_out, and_108_out, and_109_out, and_110_out, and_111_out, and_112_out, and_113_out, and_114_out, and_115_out, and_116_out, and_117_out, and_118_out, and_119_out, and_120_out, and_121_out, and_122_out);
  or or_8 (or_8_out, and_123_out, and_124_out, and_125_out, and_126_out, and_127_out, and_128_out, and_129_out, and_130_out, and_131_out, and_132_out, and_133_out, and_134_out, and_135_out, and_136_out, and_137_out, and_138_out, and_139_out);
  or or_9 (or_9_out, and_140_out, and_141_out, and_142_out, and_143_out, and_144_out, and_145_out, and_146_out, and_147_out, and_148_out, and_149_out, and_150_out, and_151_out, and_152_out, and_153_out, and_154_out, and_155_out, and_156_out);
  or or_10 (B3, and_33_out, and_34_out, and_35_out, and_36_out, and_37_out, and_38_out, and_39_out, and_40_out, and_41_out, and_42_out, and_43_out, and_44_out, and_45_out, and_46_out, and_47_out, and_48_out, and_49_out, and_50_out, and_51_out, and_52_out, and_53_out, and_54_out, and_55_out, and_56_out, and_57_out, and_58_out, and_59_out, and_60_out, and_61_out, and_62_out, and_63_out);
  or or_11 (C0, and_64_out, and_65_out, and_66_out, and_67_out, and_68_out, and_69_out, and_70_out, and_71_out, and_72_out, and_73_out, and_74_out, and_75_out, and_76_out, and_77_out, and_78_out, and_79_out, and_80_out, and_81_out, and_82_out, and_83_out, and_84_out, and_85_out, and_86_out, and_87_out, and_88_out);
  or or_12 (C1, or_6_out, or_7_out);
  or or_13 (C2, or_8_out, or_9_out);

  assign A0 = 1'b0;
  assign A1 = 1'b0;
  assign C3 = E7;
endmodule

module DECODIFICADOR (
  input  [7:0] in_1,
  output [3:0] CENTENAS,
  output [3:0] DEZENAS,
  output [3:0] UNIDADES
);

  DECODE decode_1 (
    .E0(in_1[7]), .E1(in_1[6]), .E2(in_1[5]), .E3(in_1[4]), .E4(in_1[3]), .E5(in_1[2]), .E6(in_1[1]),
    .E7(in_1[0]), .A0(CENTENAS[3]), .A1(CENTENAS[2]), .A2(CENTENAS[1]), .A3(CENTENAS[0]), .B0(DEZENAS[3]),
    .B1(DEZENAS[2]), .B2(DEZENAS[1]), .B3(DEZENAS[0]), .C0(UNIDADES[3]), .C1(UNIDADES[2]), .C2(UNIDADES[1]),
    .C3(UNIDADES[0]));
endmodule

module SUM (
  input  [7:0] \Condição_de_Parada ,
  input  [7:0] Incremento,
  input  Clock,
  input  Reset,
  output [7:0] \Saída 
);

  wire for_8_bits_1_ativado;
  wire [7:0] adder_1_out, \for_8_bits_1_saída ;

  FOR___8_bits for_8_bits_1 (
    .Clock(Clock), .Reset(Reset), .\Condição_de_Parada (\Condição_de_Parada ), .Incremento(Incremento),
    .\Saída (\for_8_bits_1_saída ), .Ativado(for_8_bits_1_ativado));
  Adder adder_1 (.a(\Saída ), .b(\for_8_bits_1_saída ), .out(adder_1_out));  // open: cin, cout
  Register register_1 (.D(adder_1_out), .Q(\Saída ), .clk(for_8_bits_1_ativado), .clr(Reset));  // open: en
endmodule

module SUM_OF_ODDS (
  input  [7:0] \Condição_de_Parada ,
  input  [7:0] Incremento,
  input  Clock,
  input  Reset,
  output [7:0] \Saída 
);

  wire for_8_bits_1_ativado, par_1_out_2;
  wire [7:0] adder_1_out, \for_8_bits_1_saída , multiplexer_1_out;

  FOR___8_bits for_8_bits_1 (
    .Clock(Clock), .Reset(Reset), .\Condição_de_Parada (\Condição_de_Parada ), .Incremento(Incremento),
    .\Saída (\for_8_bits_1_saída ), .Ativado(for_8_bits_1_ativado));
  PAR par_1 (.in_1(\for_8_bits_1_saída ), .out_2(par_1_out_2));
  Multiplexer #(.width(8), .enable("false")) multiplexer_1 (
    .in0(\for_8_bits_1_saída ), .in1({8{1'b0}}), .out(multiplexer_1_out), .sel(par_1_out_2));
  Adder adder_1 (.a(\Saída ), .b(multiplexer_1_out), .out(adder_1_out));  // open: cin, cout
  Register register_1 (.D(adder_1_out), .Q(\Saída ), .clk(for_8_bits_1_ativado), .clr(Reset));  // open: en
endmodule

module PAR (
  input  [7:0] in_1,
  output out_2
);

  not not_1 (out_2, in_1[0]);
endmodule
