// Logisim project circuito.circ as structural Verilog: 16 circuits, main circuit main
module main (
  input  in_1,
  input  in_2,
  input  in_3,
  input  in_4,
  input  in_5,
  input  in_6,
  input  in_7,
  input  in_8
);

  wire A_GANHOU, A_JOGANDO, ACERTOU, and_4_out, and_5_out, and_6_out, and_7_out, and_8_out, B_GANHOU,
       B_JOGANDO, CHUTANDO_X, CHUTANDO_Y, CHUTAR, clock_1_out, comparator_1_eq, comparator_1_gt,
       comparator_1_lt, CONFIG, core_1_s_soma, core_1_s_x, core_1_s_y, d_ff_1_qn, dma_t, dmb_t, dsa_t, dsb_t,
       EMPATE, END_A, END_B, GANHOU, IGUAL, MAIOR, MENOR, MODE, or_1_out, or_2_out, placar_1_ganhou,
       placar_2_ganhou, PROX, RESET, SA, SB, START, SX, SY, uma_t, umb_t, usa_t, usb_t;
  wire [3:0] CHUTE_X, CHUTE_Y, core_1_soma, core_1_x_real, core_1_y_real, DMA, DMB, DSA, DSB, PLACAR_A,
       PLACAR_B, SAIDA_A, SAIDA_B, SAIDA_X, SAIDA_Y, UMA, UMB, USA, USB;

  Hex_Digit_Display hex_digit_display_1 (.value(PLACAR_A));  // open: dp
  Button button_1 (.out(dma_t));
  Hex_Digit_Display hex_digit_display_2 (.value(DMA));  // open: dp
  Button button_2 (.out(uma_t));
  LED led_1 (.in(1'b1));
  LED led_2 (.in(1'b1));
  Hex_Digit_Display hex_digit_display_3 (.value(UMA));  // open: dp
  LED led_3 (.in(A_JOGANDO));
  LED led_4 (.in(SA));
  Hex_Digit_Display hex_digit_display_4 (.value(SAIDA_A));  // open: dp
  Button button_3 (.out(dsa_t));
  Button button_4 (.out(usa_t));
  Hex_Digit_Display hex_digit_display_5 (.value(USA));  // open: dp
  Hex_Digit_Display hex_digit_display_6 (.value(DSA));  // open: dp
  LED led_5 (.in(A_GANHOU));
  LED led_6 (.in(SX));
  LED led_7 (.in(MAIOR));
  Button button_5 (.out(START));
  Button button_6 (.out(PROX));
  Hex_Digit_Display hex_digit_display_7 (.value(CHUTE_X));  // open: dp
  LED led_8 (.in(CHUTANDO_X));
  LED led_9 (.in(EMPATE));
  LED led_10 (.in(ACERTOU));
  LED led_11 (.in(IGUAL));
  LED led_12 (.in(CONFIG));
  Button button_7 (.out(MODE));
  Button button_8 (.out(CHUTAR));
  LED led_13 (.in(MENOR));
  Button button_9 (.out(RESET));
  LED led_14 (.in(SY));
  LED led_15 (.in(B_GANHOU));
  Hex_Digit_Display hex_digit_display_8 (.value(CHUTE_Y));  // open: dp
  LED led_16 (.in(CHUTANDO_Y));
  Button button_10 (.out(dmb_t));
  Button button_11 (.out(umb_t));
  Hex_Digit_Display hex_digit_display_9 (.value(DMB));  // open: dp
  Hex_Digit_Display hex_digit_display_10 (.value(UMB));  // open: dp
  LED led_17 (.in(SB));
  Hex_Digit_Display hex_digit_display_11 (.value(PLACAR_B));  // open: dp
  Button button_12 (.out(dsb_t));
  LED led_18 (.in(1'b1));
  LED led_19 (.in(1'b1));
  Hex_Digit_Display hex_digit_display_12 (.value(DSB));  // open: dp
  LED led_20 (.in(B_JOGANDO));
  Hex_Digit_Display hex_digit_display_13 (.value(SAIDA_B));  // open: dp
  Button button_13 (.out(usb_t));
  Hex_Digit_Display hex_digit_display_14 (.value(USB));  // open: dp
  NEGATIVO negativo_1 (.ENTRADA({in_1, in_2, in_3, in_4}), .SAIDA(SAIDA_A), .NEG(SA));
  Comparator #(.width(4), .mode("unsigned")) comparator_1 (
    .a(PLACAR_A), .b(PLACAR_B), .gt(comparator_1_gt), .eq(comparator_1_eq), .lt(comparator_1_lt));
  and and_1 (A_GANHOU, GANHOU, comparator_1_gt);
  and and_2 (B_GANHOU, GANHOU, comparator_1_lt);
  and and_3 (EMPATE, GANHOU, comparator_1_eq);
  NEGATIVO negativo_2 (.ENTRADA({in_5, in_6, in_7, in_8}), .SAIDA(SAIDA_B), .NEG(SB));
  and and_4 (and_4_out, B_JOGANDO, ~END_A);  // AND_Gate
  or or_1 (or_1_out, and_4_out, END_B);
  and and_5 (and_5_out, ACERTOU, or_1_out);
  PLACAR placar_1 (.CLK(and_5_out), .RESET(RESET), .\SAÍDA (PLACAR_A), .GANHOU(placar_1_ganhou));
  NEGATIVO negativo_3 (.ENTRADA(SAIDA_X), .SAIDA(CHUTE_X), .NEG(SX));
  and and_6 (and_6_out, A_JOGANDO, ~END_B);  // AND_Gate
  or or_2 (or_2_out, and_6_out, END_A);
  NEGATIVO negativo_4 (.ENTRADA(SAIDA_Y), .SAIDA(CHUTE_Y), .NEG(SY));
  and and_7 (and_7_out, ACERTOU, or_2_out);
  PLACAR placar_2 (.CLK(and_7_out), .RESET(RESET), .\SAÍDA (PLACAR_B), .GANHOU(placar_2_ganhou));
  and and_8 (and_8_out, END_A, END_B);
  or or_3 (GANHOU, placar_1_ganhou, placar_2_ganhou, and_8_out);
  Clock clock_1 (.out(clock_1_out));
  RELOGIOS relogios_1 (
    .START(START), .CLK(clock_1_out), .MODE(MODE), .RESET(RESET), .SWITCH_PLAYER(CHUTANDO_X), .DMA_2(DMA),
    .UMA_2(UMA), .DSA_2(DSA), .USA_2(USA), .DMB_2(DMB), .UMB_2(UMB), .DSB_2(DSB), .USB_2(USB),
    .ZEROU_A(END_A), .ZEROU_B(END_B), .DMA(dma_t), .UMA(uma_t), .DSA(dsa_t), .USA(usa_t), .DMB(dmb_t),
    .UMB(umb_t), .DSB(dsb_t), .USB(usb_t));
  D_Flip_Flop d_ff_1 (.clk(MODE), .D(d_ff_1_qn), .Q(CONFIG), .Qn(d_ff_1_qn));  // open: preset, en, reset
  LED led_21 (.in(core_1_s_soma));
  CORE core_1 (
    .A({in_1, in_2, in_3, in_4}), .B({in_5, in_6, in_7, in_8}), .PROXIMO(PROX), .GANHOU(GANHOU),
    .ZEROU_A(END_A), .ZEROU_B(END_B), .CHUTAR(CHUTAR), .CLOCK_GERADOR(ACERTOU), .\SAÍDA_X (SAIDA_X),
    .MAIOR(MAIOR), .IGUAL(IGUAL), .MENOR(MENOR), .\SAÍDA_Y (SAIDA_Y), .X_REAL(core_1_x_real),
    .S_X(core_1_s_x), .ACERTOU(ACERTOU), .Y_REAL(core_1_y_real), .SOMA(core_1_soma), .S_Y(core_1_s_y),
    .S_SOMA(core_1_s_soma), .A_JOGANDO(A_JOGANDO), .B_JOGANDO(B_JOGANDO), .CHUTANDO_X(CHUTANDO_X),
    .CHUTANDO_Y(CHUTANDO_Y));
  LED led_22 (.in(core_1_s_x));
  Hex_Digit_Display hex_digit_display_15 (.value(core_1_soma));  // open: dp
  Hex_Digit_Display hex_digit_display_16 (.value(core_1_x_real));  // open: dp
  LED led_23 (.in(core_1_s_y));
  Hex_Digit_Display hex_digit_display_17 (.value(core_1_y_real));  // open: dp

  // Other names for the same wires on the sheet: A[3:0] = {in_1, in_2, in_3, in_4}; A0 = in_4; A1 = in_3; A2 = in_2;
  //   A3 = in_1; B[3:0] = {in_5, in_6, in_7, in_8}; B0 = in_8; B1 = in_7; B2 = in_6; B3 = in_5;
  //   CLOCK_GERADOR = ACERTOU; SWITCH_PLAYER = CHUTANDO_X; ZEROU_A = END_A; ZEROU_B = END_B

  // Notes on the sheet:
  //   JOGADOR A
  //   JOGADOR B
endmodule

// REGIS
module REGISTRADOR (
  input  [3:0] D,
  input  CLK,
  input  ENABLE,
  input  CLEAR,
  input  ACTIVATE_PRESET,
  input  [3:0] PRESET,
  output [3:0] \SAÍDA 
);

  wire and_1_out, and_2_out, and_3_out, and_4_out, or_1_out, or_2_out, or_3_out, or_4_out;
  wire [3:0] multiplexer_1_out;

  FLIP_FLOP_D flip_flop_d_1 (
    .D(D[0]), .CLK(CLK), .ENABLE(ENABLE), .PRESET(multiplexer_1_out[0]), .CLEAR(or_1_out), .Q(\SAÍDA [0]));
  or or_1 (or_1_out, and_1_out, CLEAR);
  and and_1 (and_1_out, ~multiplexer_1_out[0], ACTIVATE_PRESET);  // AND_Gate
  FLIP_FLOP_D flip_flop_d_2 (
    .D(D[1]), .CLK(CLK), .ENABLE(ENABLE), .PRESET(multiplexer_1_out[1]), .CLEAR(or_2_out), .Q(\SAÍDA [1]));
  or or_2 (or_2_out, and_2_out, CLEAR);
  and and_2 (and_2_out, ~multiplexer_1_out[1], ACTIVATE_PRESET);  // AND_Gate
  Multiplexer #(.width(4), .enable("false")) multiplexer_1 (
    .in0(4'b0000), .in1(PRESET), .out(multiplexer_1_out), .sel(ACTIVATE_PRESET));
  FLIP_FLOP_D flip_flop_d_3 (
    .D(D[2]), .CLK(CLK), .ENABLE(ENABLE), .PRESET(multiplexer_1_out[2]), .CLEAR(or_3_out), .Q(\SAÍDA [2]));
  or or_3 (or_3_out, and_3_out, CLEAR);
  and and_3 (and_3_out, ~multiplexer_1_out[2], ACTIVATE_PRESET);  // AND_Gate
  FLIP_FLOP_D flip_flop_d_4 (
    .D(D[3]), .CLK(CLK), .ENABLE(ENABLE), .PRESET(multiplexer_1_out[3]), .CLEAR(or_4_out), .Q(\SAÍDA [3]));
  or or_4 (or_4_out, and_4_out, CLEAR);
  and and_4 (and_4_out, ~multiplexer_1_out[3], ACTIVATE_PRESET);  // AND_Gate
endmodule

// FFD
module FLIP_FLOP_D (
  input  D,
  input  CLK,
  input  ENABLE,
  input  PRESET,
  input  CLEAR,
  output Q
);

  wire and_1_out, and_2_out, and_3_out, nor_2_out, not_1_out, not_2_out, not_3_out, not_4_out, or_1_out,
       or_2_out;

  not not_1 (not_1_out, CLK);
  not not_2 (not_2_out, not_3_out);
  not not_3 (not_3_out, not_1_out);
  and and_1 (and_1_out, not_2_out, CLK, ENABLE);
  not not_4 (not_4_out, D);
  and and_2 (and_2_out, not_4_out, and_1_out);
  and and_3 (and_3_out, and_1_out, D);
  or or_1 (or_1_out, CLEAR, and_2_out);
  or or_2 (or_2_out, and_3_out, PRESET);
  nor nor_1 (Q, or_1_out, nor_2_out);
  nor nor_2 (nor_2_out, Q, or_2_out);
endmodule

// PRE
module PRESET (
  input  CLK,
  input  [3:0] MAXIMO,
  input  CLEAR,
  output [3:0] \SAÍDA 
);

  wire comparator_1_eq;
  wire [3:0] adder_1_out, multiplexer_1_out;

  REGISTRADOR registrador_1 (
    .D(multiplexer_1_out), .CLK(CLK), .PRESET(4'b0000), .ENABLE(1'b1), .ACTIVATE_PRESET(1'b0), .CLEAR(CLEAR),
    .\SAÍDA (\SAÍDA ));
  Adder #(.width(4)) adder_1 (.a(\SAÍDA ), .b(4'b0001), .out(adder_1_out));  // open: cin, cout
  Comparator #(.width(4), .mode("unsigned")) comparator_1 (
    .a(adder_1_out), .b(MAXIMO), .eq(comparator_1_eq));  // open: gt, lt
  Multiplexer #(.width(4), .enable("false")) multiplexer_1 (
    .in0(adder_1_out), .in1(4'b0000), .out(multiplexer_1_out), .sel(comparator_1_eq));
endmodule

// UNI
module UNIDADES (
  input  [3:0] E,
  output [3:0] E_plus,
  output S
);

  wire and_1_out, and_2_out, and_3_out, and_4_out, and_5_out, and_6_out, and_7_out, and_8_out, and_9_out,
       and_10_out, and_11_out, and_12_out, and_13_out, and_14_out, and_15_out, not_1_out, not_2_out,
       not_3_out, not_4_out, not_5_out, not_6_out, not_7_out, not_8_out, not_9_out, not_10_out, not_11_out,
       not_12_out, not_13_out, not_14_out, not_15_out, not_16_out, not_17_out;

  not not_1 (not_1_out, E[3]);
  not not_2 (not_2_out, E[2]);
  not not_3 (not_3_out, E[1]);
  not not_4 (not_4_out, E[0]);
  not not_5 (not_5_out, E[3]);
  not not_6 (not_6_out, E[3]);
  not not_7 (not_7_out, E[2]);
  not not_8 (not_8_out, E[1]);
  not not_9 (not_9_out, E[0]);
  not not_10 (not_10_out, E[3]);
  not not_11 (not_11_out, E[3]);
  not not_12 (not_12_out, E[1]);
  not not_13 (not_13_out, E[0]);
  not not_14 (not_14_out, E[2]);
  not not_15 (not_15_out, E[1]);
  not not_16 (not_16_out, E[0]);
  not not_17 (not_17_out, E[0]);
  and and_1 (and_1_out, E[3], E[1]);
  and and_2 (and_2_out, E[3], E[2]);
  and and_3 (and_3_out, not_1_out, not_2_out, not_3_out, not_4_out);
  and and_4 (and_4_out, E[3], E[0]);
  and and_5 (and_5_out, E[3], E[1]);
  and and_6 (and_6_out, E[3], E[2]);
  and and_7 (and_7_out, not_5_out, E[2], E[0]);
  and and_8 (and_8_out, not_6_out, E[2], E[1]);
  and and_9 (and_9_out, E[3], not_7_out, not_8_out, not_9_out);
  and and_10 (and_10_out, not_10_out, E[1], E[0]);
  and and_11 (and_11_out, not_11_out, E[2], not_12_out, not_13_out);
  and and_12 (and_12_out, E[3], not_14_out, not_15_out, not_16_out);
  or or_1 (E_plus[0], not_17_out, and_1_out, and_2_out);
  and and_13 (and_13_out, E[3], E[0]);
  and and_14 (and_14_out, E[3], E[1]);
  and and_15 (and_15_out, E[3], E[2]);
  or or_2 (E_plus[3], and_3_out, and_4_out, and_5_out, and_6_out);
  or or_3 (E_plus[2], and_7_out, and_8_out, and_9_out);
  or or_4 (E_plus[1], and_10_out, and_11_out, and_12_out);
  or or_5 (S, and_13_out, and_14_out, and_15_out);
endmodule

// DEZ
module DEZENAS (
  input  [3:0] E,
  output [3:0] E_plus,
  output S
);

  wire and_1_out, and_2_out, and_3_out, and_4_out, and_5_out, and_6_out, and_7_out, and_8_out, not_1_out,
       not_2_out, not_3_out, not_4_out, not_5_out, not_6_out, not_7_out, not_8_out, not_9_out;

  not not_1 (not_1_out, E[2]);
  and and_1 (and_1_out, not_1_out, not_2_out, not_3_out);
  not not_2 (not_2_out, E[1]);
  not not_3 (not_3_out, E[0]);
  and and_2 (and_2_out, E[2], E[0]);
  and and_3 (and_3_out, E[2], E[1]);
  not not_4 (not_4_out, E[3]);
  not not_5 (not_5_out, E[2]);
  not not_6 (not_6_out, E[3]);
  not not_7 (not_7_out, E[1]);
  not not_8 (not_8_out, E[0]);
  not not_9 (not_9_out, E[0]);
  and and_4 (and_4_out, E[2], E[1]);
  and and_5 (and_5_out, E[2], E[1]);
  and and_6 (and_6_out, E[2], E[0]);
  or or_1 (E_plus[2], and_1_out, and_2_out, and_3_out, E[3]);
  and and_7 (and_7_out, not_4_out, not_5_out, E[1], E[0]);
  or or_2 (E_plus[1], and_7_out, and_8_out);
  and and_8 (and_8_out, not_6_out, E[2], not_7_out, not_8_out);
  or or_3 (E_plus[0], not_9_out, and_4_out, E[3]);
  or or_4 (S, E[3], and_5_out, and_6_out);

  assign E_plus[3] = 1'b0;
endmodule

// CONT
module CONTADOR_REGRESSIVO (
  input  CLK,
  input  [3:0] PRESET_US,
  input  [3:0] PRESET_DS,
  input  [3:0] PRESET_UM,
  input  [3:0] PRESET_DM,
  input  ENABLE,
  input  ACTIVATE_PRESET,
  input  CLEAR,
  output [3:0] US,
  output [3:0] DS,
  output [3:0] UM,
  output [3:0] DM,
  output ZEROU
);

  wire comparator_1_eq, comparator_2_eq, comparator_3_eq, comparator_4_eq, dezenas_1_s, unidades_1_s,
       unidades_2_s;
  wire [3:0] dezenas_1_e_plus, dezenas_2_e_plus, unidades_1_e_plus, unidades_2_e_plus;

  Hex_Digit_Display hex_digit_display_1 (.value(US));  // open: dp
  REGISTRADOR registrador_1 (
    .D(unidades_1_e_plus), .CLK(CLK), .PRESET(PRESET_US), .ENABLE(ENABLE), .ACTIVATE_PRESET(ACTIVATE_PRESET),
    .CLEAR(CLEAR), .\SAÍDA (US));
  UNIDADES unidades_1 (.E(US), .E_plus(unidades_1_e_plus), .S(unidades_1_s));
  REGISTRADOR registrador_2 (
    .D(dezenas_1_e_plus), .CLK(unidades_1_s), .PRESET(PRESET_DS), .ENABLE(ENABLE),
    .ACTIVATE_PRESET(ACTIVATE_PRESET), .CLEAR(CLEAR), .\SAÍDA (DS));
  Hex_Digit_Display hex_digit_display_2 (.value(DS));  // open: dp
  DEZENAS dezenas_1 (.E(DS), .E_plus(dezenas_1_e_plus), .S(dezenas_1_s));
  Hex_Digit_Display hex_digit_display_3 (.value(UM));  // open: dp
  REGISTRADOR registrador_3 (
    .D(unidades_2_e_plus), .CLK(dezenas_1_s), .PRESET(PRESET_UM), .ENABLE(ENABLE),
    .ACTIVATE_PRESET(ACTIVATE_PRESET), .CLEAR(CLEAR), .\SAÍDA (UM));
  UNIDADES unidades_2 (.E(UM), .E_plus(unidades_2_e_plus), .S(unidades_2_s));
  Hex_Digit_Display hex_digit_display_4 (.value(DM));  // open: dp
  REGISTRADOR registrador_4 (
    .D(dezenas_2_e_plus), .CLK(unidades_2_s), .PRESET(PRESET_DM), .ENABLE(ENABLE),
    .ACTIVATE_PRESET(ACTIVATE_PRESET), .CLEAR(CLEAR), .\SAÍDA (DM));
  DEZENAS dezenas_2 (.E(DM), .E_plus(dezenas_2_e_plus));  // open: S
  Comparator #(.width(4), .mode("unsigned")) comparator_1 (.a(DM), .b(4'b0000), .eq(comparator_1_eq));  // open: gt, lt
  Comparator #(.width(4), .mode("unsigned")) comparator_2 (.a(UM), .b(4'b0000), .eq(comparator_2_eq));  // open: gt, lt
  Comparator #(.width(4), .mode("unsigned")) comparator_3 (.a(DS), .b(4'b0000), .eq(comparator_3_eq));  // open: gt, lt
  Comparator #(.width(4), .mode("unsigned")) comparator_4 (.a(US), .b(4'b0000), .eq(comparator_4_eq));  // open: gt, lt
  and and_1 (ZEROU, comparator_1_eq, comparator_2_eq, comparator_3_eq, comparator_4_eq);
endmodule

// CRONO
module CRONOMETRO (
  input  CLK,
  input  CLK_DM,
  input  CLK_UM,
  input  CLK_DS,
  input  CLK_US,
  input  CLEAR_PRESET,
  input  ENABLE,
  input  ACTIVATE_PRESET,
  input  CLEAR,
  output [3:0] DM,
  output [3:0] UM,
  output [3:0] DS,
  output [3:0] US,
  output ZEROU
);

  wire and_1_out;
  wire [3:0] \preset_1_saída , \preset_2_saída , \preset_3_saída , \preset_4_saída ;

  Hex_Digit_Display hex_digit_display_1 (.value(\preset_1_saída ));  // open: dp
  PRESET preset_1 (.CLK(CLK_DM), .MAXIMO(4'b0110), .CLEAR(CLEAR_PRESET), .\SAÍDA (\preset_1_saída ));
  PRESET preset_2 (.CLK(CLK_UM), .MAXIMO(4'b1010), .CLEAR(CLEAR_PRESET), .\SAÍDA (\preset_2_saída ));
  PRESET preset_3 (.CLK(CLK_DS), .MAXIMO(4'b0110), .CLEAR(CLEAR_PRESET), .\SAÍDA (\preset_3_saída ));
  PRESET preset_4 (.CLK(CLK_US), .MAXIMO(4'b1010), .CLEAR(CLEAR_PRESET), .\SAÍDA (\preset_4_saída ));
  Hex_Digit_Display hex_digit_display_2 (.value(\preset_2_saída ));  // open: dp
  Hex_Digit_Display hex_digit_display_3 (.value(\preset_3_saída ));  // open: dp
  Hex_Digit_Display hex_digit_display_4 (.value(\preset_4_saída ));  // open: dp
  and and_1 (and_1_out, ENABLE, ~ZEROU);  // AND_Gate
  CONTADOR_REGRESSIVO contador_regressivo_1 (
    .CLK(CLK), .PRESET_US(\preset_4_saída ), .PRESET_DS(\preset_3_saída ), .PRESET_UM(\preset_2_saída ),
    .PRESET_DM(\preset_1_saída ), .US(US), .DS(DS), .UM(UM), .DM(DM), .ZEROU(ZEROU), .ENABLE(and_1_out),
    .ACTIVATE_PRESET(ACTIVATE_PRESET), .CLEAR(CLEAR));
endmodule

// CLOCKS
module RELOGIOS (
  input  DMA,
  input  UMA,
  input  DSA,
  input  USA,
  input  DMB,
  input  UMB,
  input  DSB,
  input  USB,
  input  START,
  input  CLK,
  input  MODE,
  input  RESET,
  input  SWITCH_PLAYER,
  output [3:0] DMA_2,
  output [3:0] UMA_2,
  output [3:0] DSA_2,
  output [3:0] USA_2,
  output [3:0] DMB_2,
  output [3:0] UMB_2,
  output [3:0] DSB_2,
  output [3:0] USB_2,
  output ZEROU_A,
  output ZEROU_B
);

  wire and_1_out, d_ff_1_q, d_ff_1_qn, d_ff_2_q, d_ff_2_qn, d_ff_3_q, d_ff_3_qn, multiplexer_1_out,
       multiplexer_2_out, not_1_out, or_1_out, or_2_out, or_3_out, or_4_out;

  D_Flip_Flop d_ff_1 (.clk(START), .D(d_ff_1_qn), .Q(d_ff_1_q), .Qn(d_ff_1_qn));  // open: preset, en, reset
  D_Flip_Flop d_ff_2 (.clk(MODE), .D(d_ff_2_qn), .Q(d_ff_2_q), .Qn(d_ff_2_qn));  // open: preset, en, reset
  and and_1 (and_1_out, d_ff_1_q, CLK);
  D_Flip_Flop d_ff_3 (.clk(SWITCH_PLAYER), .D(d_ff_3_qn), .Q(d_ff_3_q), .Qn(d_ff_3_qn));  // open: preset, en, reset
  or or_1 (or_1_out, DMA, DMB);
  or or_2 (or_2_out, UMA, UMB);
  or or_3 (or_3_out, DSA, DSB);
  or or_4 (or_4_out, USA, USB);
  not not_1 (not_1_out, d_ff_3_q);
  Multiplexer #(.enable("false")) multiplexer_1 (.in0(not_1_out), .in1(1'b1), .out(multiplexer_1_out), .sel(ZEROU_B));
  CRONOMETRO cronometro_1 (
    .CLK(and_1_out), .CLK_DM(or_1_out), .CLK_UM(or_2_out), .CLK_DS(or_3_out), .CLK_US(or_4_out), .DM(DMA_2),
    .UM(UMA_2), .DS(DSA_2), .US(USA_2), .ZEROU(ZEROU_A), .CLEAR_PRESET(RESET), .ENABLE(multiplexer_1_out),
    .ACTIVATE_PRESET(d_ff_2_q), .CLEAR(RESET));
  Multiplexer #(.enable("false")) multiplexer_2 (.in0(d_ff_3_q), .in1(1'b1), .out(multiplexer_2_out), .sel(ZEROU_A));
  CRONOMETRO cronometro_2 (
    .CLK(and_1_out), .CLK_DM(or_1_out), .CLK_UM(or_2_out), .CLK_DS(or_3_out), .CLK_US(or_4_out), .DM(DMB_2),
    .UM(UMB_2), .DS(DSB_2), .US(USB_2), .ZEROU(ZEROU_B), .CLEAR_PRESET(RESET), .ENABLE(multiplexer_2_out),
    .ACTIVATE_PRESET(d_ff_2_q), .CLEAR(RESET));
endmodule

// PROX
module CIRCUITO_PROXIMO (
  input  [3:0] A,
  input  ZEROU_A,
  input  [3:0] B,
  input  ZEROU_B,
  input  PROXIMO,
  output [3:0] out_6,
  output JOGADOR_ATUAL,
  output TROCA_JOGADOR,
  output CHUTANDO_Y,
  output CHUTANDO_X
);

  wire and_1_out, d_ff_1_qn;
  wire [3:0] adder_1_out, multiplexer_1_out, multiplexer_2_out, multiplexer_3_out, register_1_q;

  Register #(.width(4)) register_1 (.D(adder_1_out), .Q(register_1_q), .clk(PROXIMO), .clr(TROCA_JOGADOR));  // open: en
  Adder #(.width(4)) adder_1 (.a(register_1_q), .b(4'b0001), .out(adder_1_out));  // open: cin, cout
  Comparator #(.width(4), .mode("unsigned")) comparator_1 (
    .a(adder_1_out), .b(4'b0011), .eq(TROCA_JOGADOR));  // open: gt, lt
  Comparator #(.width(4), .mode("unsigned")) comparator_2 (
    .a(adder_1_out), .b(4'b0010), .eq(CHUTANDO_Y));  // open: gt, lt
  Comparator #(.width(4), .mode("unsigned")) comparator_3 (
    .a(adder_1_out), .b(4'b0001), .eq(CHUTANDO_X));  // open: gt, lt
  D_Flip_Flop d_ff_1 (
    .clk(TROCA_JOGADOR), .D(d_ff_1_qn), .Q(JOGADOR_ATUAL), .Qn(d_ff_1_qn));  // open: preset, en, reset
  Multiplexer #(.width(4), .enable("false")) multiplexer_1 (.in0(A), .in1(B), .out(multiplexer_1_out), .sel(ZEROU_A));
  Multiplexer #(.width(4), .enable("false")) multiplexer_2 (.in0(B), .in1(A), .out(multiplexer_2_out), .sel(ZEROU_B));
  Multiplexer #(.width(4), .enable("false")) multiplexer_3 (
    .in0(multiplexer_1_out), .in1(multiplexer_2_out), .out(multiplexer_3_out), .sel(JOGADOR_ATUAL));
  Multiplexer #(.width(4), .enable("false")) multiplexer_4 (
    .in0(multiplexer_3_out), .in1(4'b0000), .out(out_6), .sel(and_1_out));
  and and_1 (and_1_out, ZEROU_B, ZEROU_A);
  Hex_Digit_Display hex_digit_display_1 (.value(out_6));  // open: dp

  // Notes on the sheet:
  //   ESCOLHE
  //   ENTRE A E B
endmodule

// NEG
module NEGATIVO (
  input  [3:0] ENTRADA,
  output [3:0] SAIDA,
  output NEG
);

  wire and_1_out, and_2_out, and_3_out;

  and and_1 (and_1_out, ENTRADA[3], ENTRADA[0]);
  and and_2 (and_2_out, ENTRADA[3], ENTRADA[1]);
  and and_3 (and_3_out, ENTRADA[3], ENTRADA[2]);
  or or_1 (NEG, and_1_out, and_2_out, and_3_out);

  assign SAIDA = {1'b0, ENTRADA[2:0]};
endmodule

// SEL
module SELETOR (
  input  AM0,
  input  BM0,
  input  AMB,
  input  AmB_2,
  input  AIB,
  output S1,
  output S0,
  output NEG
);

  wire and_1_out, and_2_out, and_3_out, and_4_out, and_5_out, and_6_out, and_7_out, and_8_out, and_9_out,
       and_10_out, and_11_out, not_1_out, not_2_out, not_3_out, not_4_out, not_5_out, not_6_out, not_7_out,
       not_8_out, not_9_out, not_10_out, not_11_out, not_12_out, not_13_out, not_14_out, not_15_out,
       not_16_out, not_17_out, not_18_out, not_19_out, not_20_out, not_21_out, not_22_out, not_23_out,
       not_24_out, not_25_out, not_26_out, not_27_out, not_28_out, not_29_out, not_30_out, not_31_out,
       not_32_out;

  not not_1 (not_1_out, AM0);
  not not_2 (not_2_out, AMB);
  not not_3 (not_3_out, AmB_2);
  not not_4 (not_4_out, AM0);
  not not_5 (not_5_out, AMB);
  not not_6 (not_6_out, AIB);
  not not_7 (not_7_out, BM0);
  not not_8 (not_8_out, AMB);
  not not_9 (not_9_out, AmB_2);
  not not_10 (not_10_out, BM0);
  not not_11 (not_11_out, AMB);
  not not_12 (not_12_out, AIB);
  not not_13 (not_13_out, AM0);
  not not_14 (not_14_out, AMB);
  not not_15 (not_15_out, AmB_2);
  not not_16 (not_16_out, AM0);
  not not_17 (not_17_out, AmB_2);
  not not_18 (not_18_out, AIB);
  not not_19 (not_19_out, BM0);
  not not_20 (not_20_out, AMB);
  not not_21 (not_21_out, AmB_2);
  not not_22 (not_22_out, BM0);
  not not_23 (not_23_out, AmB_2);
  not not_24 (not_24_out, AIB);
  not not_25 (not_25_out, AM0);
  not not_26 (not_26_out, BM0);
  not not_27 (not_27_out, BM0);
  not not_28 (not_28_out, AMB);
  not not_29 (not_29_out, AIB);
  not not_30 (not_30_out, AM0);
  not not_31 (not_31_out, AmB_2);
  not not_32 (not_32_out, AIB);
  and and_1 (and_1_out, not_1_out, BM0, not_2_out, not_3_out, AIB);
  and and_2 (and_2_out, not_4_out, BM0, not_5_out, AmB_2, not_6_out);
  and and_3 (and_3_out, AM0, not_7_out, not_8_out, not_9_out, AIB);
  and and_4 (and_4_out, AM0, not_10_out, not_11_out, AmB_2, not_12_out);
  and and_5 (and_5_out, not_13_out, BM0, not_14_out, not_15_out, AIB);
  and and_6 (and_6_out, not_16_out, BM0, AMB, not_17_out, not_18_out);
  and and_7 (and_7_out, AM0, not_19_out, not_20_out, not_21_out, AIB);
  and and_8 (and_8_out, AM0, not_22_out, AMB, not_23_out, not_24_out);
  and and_9 (and_9_out, not_25_out, not_26_out);
  and and_10 (and_10_out, not_27_out, not_28_out, AmB_2, not_29_out);
  and and_11 (and_11_out, not_30_out, AMB, not_31_out, not_32_out);
  or or_1 (S1, and_1_out, and_2_out, and_3_out, and_4_out);
  or or_2 (S0, and_5_out, and_6_out, and_7_out, and_8_out);
  or or_3 (NEG, and_9_out, and_10_out, and_11_out);
endmodule

// SUM
module SOMA_NEG (
  input  [3:0] A,
  input  [3:0] B,
  output [3:0] SAIDA,
  output NEG
);

  wire comparator_1_eq, comparator_1_gt, comparator_1_lt, negativo_1_neg, negativo_2_neg, not_1_out,
       not_2_out;
  wire [1:0] seletor_1_s0;
  wire [3:0] adder_1_out, negativo_1_saida, negativo_2_saida, subtractor_1_out, subtractor_2_out;

  NEGATIVO negativo_1 (.ENTRADA(A), .SAIDA(negativo_1_saida), .NEG(negativo_1_neg));
  NEGATIVO negativo_2 (.ENTRADA(B), .SAIDA(negativo_2_saida), .NEG(negativo_2_neg));
  not not_1 (not_1_out, negativo_1_neg);
  not not_2 (not_2_out, negativo_2_neg);
  Adder #(.width(4)) adder_1 (.a(negativo_1_saida), .b(negativo_2_saida), .out(adder_1_out));  // open: cin, cout
  Subtractor #(.width(4)) subtractor_1 (
    .a(negativo_1_saida), .b(negativo_2_saida), .out(subtractor_1_out));  // open: bin, bout
  Subtractor #(.width(4)) subtractor_2 (
    .a(negativo_2_saida), .b(negativo_1_saida), .out(subtractor_2_out));  // open: bin, bout
  Comparator #(.width(4)) comparator_1 (
    .a(negativo_1_saida), .b(negativo_2_saida), .gt(comparator_1_gt), .eq(comparator_1_eq),
    .lt(comparator_1_lt));
  SELETOR seletor_1 (
    .AM0(not_1_out), .BM0(not_2_out), .AMB(comparator_1_gt), .AmB_2(comparator_1_lt), .AIB(comparator_1_eq),
    .S1(seletor_1_s0[1]), .S0(seletor_1_s0[0]), .NEG(NEG));
  Multiplexer #(.select(2), .width(4), .enable("false")) multiplexer_1 (
    .in0(adder_1_out), .in1(subtractor_1_out), .in2(subtractor_2_out), .in3(4'b0000), .out(SAIDA),
    .sel(seletor_1_s0));

  // Notes on the sheet:
  //   SE A>0 E B<0:
  //   SE A<0 E B>0:
  //   SE A>0 E B>0 : RETORNA +(A+B)
  //   SE A<0 E B<0 : RETORNA -(A+B)
  //   SE A>B: RETORNA A-B
  //   SE A= B: RETORNA 0
  //   SE A<B: RETORNA -(B-A)
  //   SE A>B: RETORNA -(A-B)
  //   SE A= B: RETORNA 0
  //   SE A<B: RETORNA B-A
endmodule

module CORE (
  input  [3:0] A,
  input  [3:0] B,
  input  PROXIMO,
  input  GANHOU,
  input  ZEROU_A,
  input  ZEROU_B,
  input  CHUTAR,
  input  CLOCK_GERADOR,
  output A_JOGANDO,
  output [3:0] \SAÍDA_X ,
  output MAIOR,
  output IGUAL,
  output MENOR,
  output [3:0] \SAÍDA_Y ,
  output B_JOGANDO,
  output [3:0] X_REAL,
  output S_X,
  output ACERTOU,
  output CHUTANDO_X,
  output CHUTANDO_Y,
  output [3:0] Y_REAL,
  output [3:0] SOMA,
  output S_Y,
  output S_SOMA
);

  wire and_1_out, and_2_out, and_3_out, circuito_proximo_1_troca_jogador, comparador_2_igual,
       comparador_3_igual, JOGADOR_ATUAL, negativo_3_neg, negativo_4_neg, negativo_5_neg, negativo_6_neg,
       not_1_out, or_1_out, or_2_out, soma_neg_2_neg;
  wire [0:0] and_5_out, and_6_out;
  wire [3:0] circuito_proximo_1_out_6, negativo_3_saida, negativo_4_saida, negativo_5_saida,
       negativo_6_saida, random_1_out, random_2_out, soma_neg_2_saida;

  and and_1 (and_1_out, PROXIMO, ~GANHOU);  // AND_Gate
  CIRCUITO_PROXIMO circuito_proximo_1 (
    .A(A), .ZEROU_A(ZEROU_A), .B(B), .ZEROU_B(ZEROU_B), .PROXIMO(and_1_out),
    .out_6(circuito_proximo_1_out_6), .JOGADOR_ATUAL(JOGADOR_ATUAL),
    .TROCA_JOGADOR(circuito_proximo_1_troca_jogador), .CHUTANDO_Y(CHUTANDO_Y), .CHUTANDO_X(CHUTANDO_X));
  and and_2 (and_2_out, CHUTANDO_X, CHUTAR);
  and and_3 (and_3_out, CHUTAR, CHUTANDO_Y);
  Register #(.width(4)) register_1 (.D(circuito_proximo_1_out_6), .Q(\SAÍDA_X ), .clk(or_1_out));  // open: en, clr
  or or_1 (or_1_out, CHUTANDO_Y, and_2_out);
  Register #(.width(4)) register_2 (.D(circuito_proximo_1_out_6), .Q(\SAÍDA_Y ), .clk(or_2_out));  // open: en, clr
  or or_2 (or_2_out, circuito_proximo_1_troca_jogador, and_3_out);
  Random #(.width(4)) random_1 (.clk(CLOCK_GERADOR), .out(random_1_out));  // open: next, clr
  Random #(.width(4)) random_2 (.clk(CLOCK_GERADOR), .out(random_2_out), .clr(CLOCK_GERADOR));  // open: next
  NEGATIVO negativo_1 (.ENTRADA(random_1_out), .SAIDA(X_REAL), .NEG(S_X));
  SOMA_NEG soma_neg_1 (.A(random_1_out), .B(random_2_out), .SAIDA(SOMA), .NEG(S_SOMA));
  NEGATIVO negativo_2 (.ENTRADA(random_2_out), .SAIDA(Y_REAL), .NEG(S_Y));
  SOMA_NEG soma_neg_2 (.A(\SAÍDA_X ), .B(\SAÍDA_Y ), .SAIDA(soma_neg_2_saida), .NEG(soma_neg_2_neg));
  COMPARADOR comparador_1 (
    .A_NEG(soma_neg_2_neg), .A(soma_neg_2_saida), .B_NEG(S_SOMA), .B(SOMA), .ENABLE(CHUTANDO_X),
    .MAIOR(MAIOR), .IGUAL(IGUAL), .MENOR(MENOR));
  NEGATIVO negativo_3 (.ENTRADA(\SAÍDA_X ), .SAIDA(negativo_3_saida), .NEG(negativo_3_neg));
  NEGATIVO negativo_4 (.ENTRADA(random_1_out), .SAIDA(negativo_4_saida), .NEG(negativo_4_neg));
  NEGATIVO negativo_5 (.ENTRADA(\SAÍDA_Y ), .SAIDA(negativo_5_saida), .NEG(negativo_5_neg));
  NEGATIVO negativo_6 (.ENTRADA(random_2_out), .SAIDA(negativo_6_saida), .NEG(negativo_6_neg));
  COMPARADOR comparador_2 (
    .A_NEG(negativo_3_neg), .A(negativo_3_saida), .B_NEG(negativo_4_neg), .B(negativo_4_saida),
    .ENABLE(1'b1), .IGUAL(comparador_2_igual));  // open: MAIOR, MENOR
  COMPARADOR comparador_3 (
    .A_NEG(negativo_5_neg), .A(negativo_5_saida), .B_NEG(negativo_6_neg), .B(negativo_6_saida),
    .ENABLE(1'b1), .IGUAL(comparador_3_igual));  // open: MAIOR, MENOR
  and and_4 (ACERTOU, comparador_2_igual, comparador_3_igual);
  not not_1 (not_1_out, JOGADOR_ATUAL);
  and and_5 (and_5_out[0], ZEROU_B, ~ZEROU_A);  // AND_Gate
  and and_6 (and_6_out[0], ZEROU_A, ~ZEROU_B);  // AND_Gate
  Multiplexer #(.select(2), .enable("false")) multiplexer_1 (
    .in0(not_1_out), .in1(1'b1), .in2(1'b0), .out(A_JOGANDO), .sel({ZEROU_A, and_5_out[0]}));  // open: in3
  Multiplexer #(.select(2), .enable("false")) multiplexer_2 (
    .in0(JOGADOR_ATUAL), .in1(1'b1), .in2(1'b0), .out(B_JOGANDO), .sel({ZEROU_B, and_6_out[0]}));  // open: in3

  // Notes on the sheet:
  //   REGISTRA X
  //   REGISTRA Y
endmodule

// COMP
module COMPARADOR (
  input  A_NEG,
  input  [3:0] A,
  input  B_NEG,
  input  [3:0] B,
  input  ENABLE,
  output MAIOR,
  output IGUAL,
  output MENOR
);

  wire and_1_out, and_2_out, and_3_out, and_4_out, and_5_out, and_6_out, and_7_out, and_8_out,
       comparator_1_gt, comparator_2_lt, comparator_3_lt, comparator_4_gt, comparator_5_eq, or_1_out,
       or_2_out, or_3_out;

  LED led_1 (.in(A_NEG));
  Hex_Digit_Display hex_digit_display_1 (.value(A));  // open: dp
  LED led_2 (.in(B_NEG));
  Hex_Digit_Display hex_digit_display_2 (.value(B));  // open: dp
  and and_1 (and_1_out, A_NEG, ~B_NEG);  // AND_Gate
  Comparator #(.width(4), .mode("unsigned")) comparator_1 (.a(A), .b(B), .gt(comparator_1_gt));  // open: eq, lt
  Comparator #(.width(4), .mode("unsigned")) comparator_2 (.a(A), .b(B), .lt(comparator_2_lt));  // open: gt, eq
  Comparator #(.width(4), .mode("unsigned")) comparator_3 (.a(A), .b(B), .lt(comparator_3_lt));  // open: gt, eq
  Comparator #(.width(4), .mode("unsigned")) comparator_4 (.a(A), .b(B), .gt(comparator_4_gt));  // open: eq, lt
  Comparator #(.width(4), .mode("unsigned")) comparator_5 (.a(A), .b(B), .eq(comparator_5_eq));  // open: gt, lt
  and and_2 (and_2_out, ~A_NEG, B_NEG);  // AND_Gate
  and and_3 (and_3_out, A_NEG, B_NEG, comparator_3_lt);
  and and_4 (and_4_out, ~A_NEG, ~B_NEG, comparator_4_gt);  // AND_Gate
  and and_5 (and_5_out, A_NEG, B_NEG, comparator_1_gt);
  and and_6 (and_6_out, ~A_NEG, ~B_NEG, comparator_2_lt);  // AND_Gate
  and and_7 (and_7_out, comparator_5_eq, A_NEG, B_NEG);
  and and_8 (and_8_out, comparator_5_eq, ~A_NEG, ~B_NEG);  // AND_Gate
  or or_1 (or_1_out, and_2_out, and_3_out, and_4_out);
  or or_2 (or_2_out, and_7_out, and_8_out);
  or or_3 (or_3_out, and_5_out, and_6_out, and_1_out);
  and and_9 (MAIOR, or_1_out, ENABLE);
  and and_10 (IGUAL, or_2_out, ENABLE);
  and and_11 (MENOR, or_3_out, ENABLE);
endmodule

module PLACAR (
  input  CLK,
  input  RESET,
  output [3:0] \SAÍDA ,
  output GANHOU
);

  wire [3:0] adder_1_out;

  Register #(.width(4)) register_1 (.D(adder_1_out), .Q(\SAÍDA ), .clk(CLK), .clr(RESET));  // open: en
  Adder #(.width(4)) adder_1 (.a(\SAÍDA ), .b(4'b0001), .out(adder_1_out));  // open: cin, cout
  Comparator #(.width(4), .mode("unsigned")) comparator_1 (.a(\SAÍDA ), .b(4'b1111), .eq(GANHOU));  // open: gt, lt
endmodule
