// Logisim project SOMADOR-4-BITS.circ as structural Verilog: 4 circuits, main circuit main
module main (
  input  A0,
  input  A1,
  input  A2,
  input  A3,
  input  B0,
  input  B1,
  input  B2,
  input  B3,
  output _1,
  output _2,
  output _4,
  output _8,
  output _16
);

  SOMADOR_4_BITS somador_4_bits_1 (
    .A0(A0), .A1(A1), .A2(A2), .A3(A3), .B0(B0), .B1(B1), .B2(B2), .B3(B3), ._1(_1), ._2(_2), ._4(_4),
    ._8(_8), ._16(_16));

  // Notes on the sheet:
  //   Entrada A
  //   Entrada B
endmodule

module XOR (
  input  in_1,
  input  in_2,
  output out_3
);

  wire and_1_out, and_2_out, not_1_out, not_2_out;

  not not_1 (not_1_out, in_2);
  not not_2 (not_2_out, in_1);
  and and_1 (and_1_out, in_1, not_1_out);
  and and_2 (and_2_out, not_2_out, in_2);
  or or_1 (out_3, and_1_out, and_2_out);
endmodule

module SOMADOR_2_BITS (
  input  A,
  input  B,
  input  C,
  output S,
  output CARRY
);

  wire and_1_out, and_2_out, xor_1_out_3;

  XOR xor_1 (.in_1(A), .in_2(B), .out_3(xor_1_out_3));
  and and_1 (and_1_out, A, B);
  XOR xor_2 (.in_1(xor_1_out_3), .in_2(C), .out_3(S));
  and and_2 (and_2_out, xor_1_out_3, C);
  or or_1 (CARRY, and_1_out, and_2_out);
endmodule

module SOMADOR_4_BITS (
  input  A0,
  input  A1,
  input  A2,
  input  A3,
  input  B0,
  input  B1,
  input  B2,
  input  B3,
  output _1,
  output _2,
  output _4,
  output _8,
  output _16
);

  wire somador_2_bits_1_carry, somador_2_bits_2_carry, somador_2_bits_3_carry;

  SOMADOR_2_BITS somador_2_bits_1 (.A(A0), .B(B0), .C(1'b0), .S(_1), .CARRY(somador_2_bits_1_carry));
  SOMADOR_2_BITS somador_2_bits_2 (.A(A1), .B(B1), .C(somador_2_bits_1_carry), .S(_2), .CARRY(somador_2_bits_2_carry));
  SOMADOR_2_BITS somador_2_bits_3 (.A(A2), .B(B2), .C(somador_2_bits_2_carry), .S(_4), .CARRY(somador_2_bits_3_carry));
  SOMADOR_2_BITS somador_2_bits_4 (.A(A3), .B(B3), .C(somador_2_bits_3_carry), .S(_8), .CARRY(_16));

  // Notes on the sheet:
  //   Entrada A
  //   Entrada B
endmodule
